// Logisim project Natanael_Bezerra.circ as structural Verilog: 6 circuits, main circuit main
module main (
  input  [7:0] A,
  input  WE,
  input  OE,
  input  clk,
  input  [7:0] D,
  output [7:0] out_6,
  output [7:0] out_7
);

  RAM ram_1 (.addr(A), .we(WE), .oe(OE), .clk(clk), .din(D), .dout(out_6));
  ram4x4 ram4x4_1 (.A(A), .clk(clk), .WE(WE), .OE(OE), .D(D), .D_out(out_7));
endmodule

// 1b
module flipD (
  input  iput,
  input  set,
  output sout
);

  wire nand_1_out, nand_2_out, nand_4_out, not_1_out;

  not not_1 (not_1_out, iput);
  nand nand_1 (nand_1_out, iput, set);
  nand nand_2 (nand_2_out, set, not_1_out);
  nand nand_3 (sout, nand_1_out, nand_4_out);
  nand nand_4 (nand_4_out, sout, nand_2_out);
endmodule

// reg
module reg8 (
  input  [7:0] sinput,
  input  set,
  input  endble,
  output [7:0] sout
);

  wire flipd_1_sout, flipd_2_sout, flipd_3_sout, flipd_4_sout, flipd_5_sout, flipd_6_sout, flipd_7_sout,
       flipd_8_sout;

  flipD flipd_1 (.iput(sinput[0]), .set(set), .sout(flipd_1_sout));
  flipD flipd_2 (.iput(sinput[1]), .set(set), .sout(flipd_2_sout));
  flipD flipd_3 (.iput(sinput[2]), .set(set), .sout(flipd_3_sout));
  flipD flipd_4 (.iput(sinput[3]), .set(set), .sout(flipd_4_sout));
  flipD flipd_5 (.iput(sinput[4]), .set(set), .sout(flipd_5_sout));
  flipD flipd_6 (.iput(sinput[5]), .set(set), .sout(flipd_6_sout));
  flipD flipd_7 (.iput(sinput[6]), .set(set), .sout(flipd_7_sout));
  flipD flipd_8 (.iput(sinput[7]), .set(set), .sout(flipd_8_sout));
  and and_1 (sout[0], flipd_1_sout, endble);
  and and_2 (sout[1], flipd_2_sout, endble);
  and and_3 (sout[2], flipd_3_sout, endble);
  and and_4 (sout[3], flipd_4_sout, endble);
  and and_5 (sout[4], flipd_5_sout, endble);
  and and_6 (sout[5], flipd_6_sout, endble);
  and and_7 (sout[6], flipd_7_sout, endble);
  and and_8 (sout[7], flipd_8_sout, endble);
endmodule

// cell
module cell_memo (
  input  x,
  input  [7:0] dt_in,
  input  y,
  input  set,
  input  clk,
  output [7:0] dt_out
);

  wire and_1_out, and_2_out, and_3_out;
  wire [7:0] reg8_1_sout;

  and and_1 (and_1_out, x, y);
  and and_2 (and_2_out, and_1_out, set);
  and and_3 (and_3_out, and_1_out, clk);
  reg8 reg8_1 (.sinput(dt_in), .set(and_2_out), .endble(and_3_out), .sout(reg8_1_sout));
  assign dt_out = and_3_out ? reg8_1_sout : 8'bz;  // Controlled_Buffer controlled_buffer_1
endmodule

module ram4x4 (
  input  [7:0] A,
  input  clk,
  input  WE,
  input  OE,
  input  [7:0] D,
  output [7:0] D_out
);

  wire and_1_out, and_2_out, and_3_out, and_4_out, and_5_out, and_6_out, decoder_1_out0, decoder_1_out1,
       decoder_1_out2, decoder_1_out3, decoder_2_out0, decoder_2_out1, decoder_2_out2, decoder_2_out3,
       not_1_out, not_2_out;
  wire [7:0] cell_memo_1_dt_out, cell_memo_5_dt_out, cell_memo_9_dt_out, cell_memo_13_dt_out,
       controlled_buffer_1_out, controlled_buffer_2_out, controlled_buffer_4_out, controlled_buffer_6_out,
       controlled_buffer_8_out;

  Decoder #(.enable("false"), .select(4)) decoder_1 (
    .out0(decoder_1_out0), .out1(decoder_1_out1), .out2(decoder_1_out2), .out3(decoder_1_out3), .sel(A[7:4]));  // open: out4, out5, out6, out7, out8, out9, out10, out11, out12, out13, out14, out15
  and and_1 (and_1_out, WE, clk);
  and and_2 (and_2_out, clk, OE);
  not not_1 (not_1_out, and_2_out);
  assign controlled_buffer_1_out = not_2_out ? controlled_buffer_2_out : 8'bz;  // Controlled_Buffer controlled_buffer_1
  not not_2 (not_2_out, OE);
  assign controlled_buffer_2_out = not_2_out ? D : 8'bz;  // Controlled_Buffer controlled_buffer_2
  cell_memo cell_memo_1 (
    .dt_in(controlled_buffer_1_out), .y(decoder_2_out0), .set(and_1_out), .clk(clk), .x(decoder_1_out0),
    .dt_out(cell_memo_1_dt_out));
  cell_memo cell_memo_2 (
    .dt_in(controlled_buffer_1_out), .y(decoder_2_out0), .set(and_1_out), .clk(clk), .x(decoder_1_out1),
    .dt_out(cell_memo_1_dt_out));
  cell_memo cell_memo_3 (
    .dt_in(controlled_buffer_1_out), .y(decoder_2_out0), .set(and_1_out), .clk(clk), .x(decoder_1_out2),
    .dt_out(cell_memo_1_dt_out));
  cell_memo cell_memo_4 (
    .dt_in(controlled_buffer_1_out), .y(decoder_2_out0), .set(and_1_out), .clk(clk), .x(decoder_1_out3),
    .dt_out(cell_memo_1_dt_out));
  and and_3 (and_3_out, OE, decoder_2_out0);
  assign controlled_buffer_2_out = and_3_out ? cell_memo_1_dt_out : 8'bz;  // Controlled_Buffer controlled_buffer_3
  Decoder #(.enable("false"), .select(4)) decoder_2 (
    .out0(decoder_2_out0), .out1(decoder_2_out1), .out2(decoder_2_out2), .out3(decoder_2_out3), .sel(A[3:0]));  // open: out4, out5, out6, out7, out8, out9, out10, out11, out12, out13, out14, out15
  assign controlled_buffer_4_out = not_2_out ? controlled_buffer_2_out : 8'bz;  // Controlled_Buffer controlled_buffer_4
  cell_memo cell_memo_5 (
    .dt_in(controlled_buffer_4_out), .y(decoder_2_out1), .set(and_1_out), .clk(clk), .x(decoder_1_out0),
    .dt_out(cell_memo_5_dt_out));
  cell_memo cell_memo_6 (
    .dt_in(controlled_buffer_4_out), .y(decoder_2_out1), .set(and_1_out), .clk(clk), .x(decoder_1_out1),
    .dt_out(cell_memo_5_dt_out));
  cell_memo cell_memo_7 (
    .dt_in(controlled_buffer_4_out), .y(decoder_2_out1), .set(and_1_out), .clk(clk), .x(decoder_1_out2),
    .dt_out(cell_memo_5_dt_out));
  cell_memo cell_memo_8 (
    .dt_in(controlled_buffer_4_out), .y(decoder_2_out1), .set(and_1_out), .clk(clk), .x(decoder_1_out3),
    .dt_out(cell_memo_5_dt_out));
  and and_4 (and_4_out, OE, decoder_2_out1);
  assign controlled_buffer_2_out = and_4_out ? cell_memo_5_dt_out : 8'bz;  // Controlled_Buffer controlled_buffer_5
  assign controlled_buffer_6_out = not_2_out ? controlled_buffer_2_out : 8'bz;  // Controlled_Buffer controlled_buffer_6
  cell_memo cell_memo_9 (
    .dt_in(controlled_buffer_6_out), .y(decoder_2_out2), .set(and_1_out), .clk(clk), .x(decoder_1_out0),
    .dt_out(cell_memo_9_dt_out));
  cell_memo cell_memo_10 (
    .dt_in(controlled_buffer_6_out), .y(decoder_2_out2), .set(and_1_out), .clk(clk), .x(decoder_1_out1),
    .dt_out(cell_memo_9_dt_out));
  cell_memo cell_memo_11 (
    .dt_in(controlled_buffer_6_out), .y(decoder_2_out2), .set(and_1_out), .clk(clk), .x(decoder_1_out2),
    .dt_out(cell_memo_9_dt_out));
  cell_memo cell_memo_12 (
    .dt_in(controlled_buffer_6_out), .y(decoder_2_out2), .set(and_1_out), .clk(clk), .x(decoder_1_out3),
    .dt_out(cell_memo_9_dt_out));
  and and_5 (and_5_out, OE, decoder_2_out2);
  assign controlled_buffer_2_out = and_5_out ? cell_memo_9_dt_out : 8'bz;  // Controlled_Buffer controlled_buffer_7
  assign controlled_buffer_8_out = not_2_out ? controlled_buffer_2_out : 8'bz;  // Controlled_Buffer controlled_buffer_8
  cell_memo cell_memo_13 (
    .dt_in(controlled_buffer_8_out), .y(decoder_2_out3), .set(and_1_out), .clk(clk), .x(decoder_1_out0),
    .dt_out(cell_memo_13_dt_out));
  cell_memo cell_memo_14 (
    .dt_in(controlled_buffer_8_out), .y(decoder_2_out3), .set(and_1_out), .clk(clk), .x(decoder_1_out1),
    .dt_out(cell_memo_13_dt_out));
  cell_memo cell_memo_15 (
    .dt_in(controlled_buffer_8_out), .y(decoder_2_out3), .set(and_1_out), .clk(clk), .x(decoder_1_out2),
    .dt_out(cell_memo_13_dt_out));
  cell_memo cell_memo_16 (
    .dt_in(controlled_buffer_8_out), .y(decoder_2_out3), .set(and_1_out), .clk(clk), .x(decoder_1_out3),
    .dt_out(cell_memo_13_dt_out));
  and and_6 (and_6_out, OE, decoder_2_out3);
  assign controlled_buffer_2_out = and_6_out ? cell_memo_13_dt_out : 8'bz;  // Controlled_Buffer controlled_buffer_9
  Register register_1 (.D(controlled_buffer_2_out), .Q(D_out), .clk(not_1_out));  // open: en, clr
endmodule

module modelo (
);

  wire undriven, undriven_3, undriven_4, undriven_5, undriven_7, undriven_8, undriven_9, undriven_11,
       undriven_12, undriven_13, undriven_15, undriven_16, undriven_17, undriven_18, undriven_19, undriven_20;
  wire [7:0] cell_memo_1_dt_out, cell_memo_5_dt_out, cell_memo_9_dt_out, cell_memo_13_dt_out, undriven_2,
       undriven_6, undriven_10, undriven_14;

  cell_memo cell_memo_1 (
    .dt_in(undriven_2), .y(undriven), .set(undriven_3), .clk(undriven_4), .x(undriven_17),
    .dt_out(cell_memo_1_dt_out));
  cell_memo cell_memo_2 (
    .dt_in(undriven_2), .y(undriven), .set(undriven_3), .clk(undriven_4), .x(undriven_18),
    .dt_out(cell_memo_1_dt_out));
  cell_memo cell_memo_3 (
    .dt_in(undriven_2), .y(undriven), .set(undriven_3), .clk(undriven_4), .x(undriven_19),
    .dt_out(cell_memo_1_dt_out));
  cell_memo cell_memo_4 (
    .dt_in(undriven_2), .y(undriven), .set(undriven_3), .clk(undriven_4), .x(undriven_20),
    .dt_out(cell_memo_1_dt_out));
  cell_memo cell_memo_5 (
    .dt_in(undriven_6), .y(undriven_5), .set(undriven_7), .clk(undriven_8), .x(undriven_17),
    .dt_out(cell_memo_5_dt_out));
  cell_memo cell_memo_6 (
    .dt_in(undriven_6), .y(undriven_5), .set(undriven_7), .clk(undriven_8), .x(undriven_18),
    .dt_out(cell_memo_5_dt_out));
  cell_memo cell_memo_7 (
    .dt_in(undriven_6), .y(undriven_5), .set(undriven_7), .clk(undriven_8), .x(undriven_19),
    .dt_out(cell_memo_5_dt_out));
  cell_memo cell_memo_8 (
    .dt_in(undriven_6), .y(undriven_5), .set(undriven_7), .clk(undriven_8), .x(undriven_20),
    .dt_out(cell_memo_5_dt_out));
  cell_memo cell_memo_9 (
    .dt_in(undriven_10), .y(undriven_9), .set(undriven_11), .clk(undriven_12), .x(undriven_17),
    .dt_out(cell_memo_9_dt_out));
  cell_memo cell_memo_10 (
    .dt_in(undriven_10), .y(undriven_9), .set(undriven_11), .clk(undriven_12), .x(undriven_18),
    .dt_out(cell_memo_9_dt_out));
  cell_memo cell_memo_11 (
    .dt_in(undriven_10), .y(undriven_9), .set(undriven_11), .clk(undriven_12), .x(undriven_19),
    .dt_out(cell_memo_9_dt_out));
  cell_memo cell_memo_12 (
    .dt_in(undriven_10), .y(undriven_9), .set(undriven_11), .clk(undriven_12), .x(undriven_20),
    .dt_out(cell_memo_9_dt_out));
  cell_memo cell_memo_13 (
    .dt_in(undriven_14), .y(undriven_13), .set(undriven_15), .clk(undriven_16), .x(undriven_17),
    .dt_out(cell_memo_13_dt_out));
  cell_memo cell_memo_14 (
    .dt_in(undriven_14), .y(undriven_13), .set(undriven_15), .clk(undriven_16), .x(undriven_18),
    .dt_out(cell_memo_13_dt_out));
  cell_memo cell_memo_15 (
    .dt_in(undriven_14), .y(undriven_13), .set(undriven_15), .clk(undriven_16), .x(undriven_19),
    .dt_out(cell_memo_13_dt_out));
  cell_memo cell_memo_16 (
    .dt_in(undriven_14), .y(undriven_13), .set(undriven_15), .clk(undriven_16), .x(undriven_20),
    .dt_out(cell_memo_13_dt_out));
endmodule
