// Logisim project ULA.circ as structural Verilog: 10 circuits, main circuit main
module main (
  input  in_1,
  input  in_2,
  input  in_3,
  input  in_4,
  input  [7:0] in_5,
  input  in_6,
  input  [7:0] in_7,
  input  [7:0] in_8,
  input  [2:0] in_9,
  output [7:0] out_10,
  output out_11,
  output [7:0] out_12,
  output zero,
  output a_large_b,
  output iquals
);

  wire [7:0] reg2_1_out_4, register_1_q;

  reg2 reg2_1 (.in_1(reg2_1_out_4), .out_4(reg2_1_out_4));  // open: clk, buffer_endble
  reg2 reg2_2 (.in_1(reg2_1_out_4), .out_4(reg2_1_out_4));  // open: clk, buffer_endble
  reg2 reg2_3 (.in_1(reg2_1_out_4), .out_4(reg2_1_out_4));  // open: clk, buffer_endble
  ULAT ulat_1 (
    .A(in_8), .B(in_7), .carry_in(in_6), .carry_out(out_11), .sout(out_12), .func(in_9), .zero(zero),
    .a_large(a_large_b), .iquals(iquals));
  reg2 reg2_4 (.in_1(reg2_1_out_4), .out_4(reg2_1_out_4));  // open: clk, buffer_endble
  Register register_1 (.D(reg2_1_out_4), .Q(register_1_q), .clk(in_1));  // open: en, clr
  RAM ram_1 (.addr(register_1_q), .we(in_2), .oe(in_3), .clk(in_4), .din(in_5), .dout(out_10));
endmodule

// 1b
module flipD (
  input  iput,
  input  set,
  output sout
);

  wire nand_1_out, nand_2_out, nand_4_out, not_1_out;

  not not_1 (not_1_out, iput);
  nand nand_1 (nand_1_out, iput, set);
  nand nand_2 (nand_2_out, set, not_1_out);
  nand nand_3 (sout, nand_1_out, nand_4_out);
  nand nand_4 (nand_4_out, sout, nand_2_out);
endmodule

// reg
module reg8 (
  input  [7:0] sinput,
  input  set,
  input  endble,
  output [7:0] sout
);

  wire flipd_1_sout, flipd_2_sout, flipd_3_sout, flipd_4_sout, flipd_5_sout, flipd_6_sout, flipd_7_sout,
       flipd_8_sout;

  flipD flipd_1 (.iput(sinput[0]), .set(set), .sout(flipd_1_sout));
  flipD flipd_2 (.iput(sinput[1]), .set(set), .sout(flipd_2_sout));
  flipD flipd_3 (.iput(sinput[2]), .set(set), .sout(flipd_3_sout));
  flipD flipd_4 (.iput(sinput[3]), .set(set), .sout(flipd_4_sout));
  flipD flipd_5 (.iput(sinput[4]), .set(set), .sout(flipd_5_sout));
  flipD flipd_6 (.iput(sinput[5]), .set(set), .sout(flipd_6_sout));
  flipD flipd_7 (.iput(sinput[6]), .set(set), .sout(flipd_7_sout));
  flipD flipd_8 (.iput(sinput[7]), .set(set), .sout(flipd_8_sout));
  and and_1 (sout[0], flipd_1_sout, endble);
  and and_2 (sout[1], flipd_2_sout, endble);
  and and_3 (sout[2], flipd_3_sout, endble);
  and and_4 (sout[3], flipd_4_sout, endble);
  and and_5 (sout[4], flipd_5_sout, endble);
  and and_6 (sout[5], flipd_6_sout, endble);
  and and_7 (sout[6], flipd_7_sout, endble);
  and and_8 (sout[7], flipd_8_sout, endble);
endmodule

// cell
module cell_memo (
  input  x,
  input  [7:0] dt_in,
  input  y,
  input  set,
  input  clk,
  output [7:0] dt_out
);

  wire and_1_out, and_2_out, and_3_out;
  wire [7:0] reg8_1_sout;

  and and_1 (and_1_out, x, y);
  and and_2 (and_2_out, and_1_out, set);
  and and_3 (and_3_out, and_1_out, clk);
  reg8 reg8_1 (.sinput(dt_in), .set(and_2_out), .endble(and_3_out), .sout(reg8_1_sout));
  assign dt_out = and_3_out ? reg8_1_sout : 8'bz;  // Controlled_Buffer controlled_buffer_1
endmodule

module ram4x4 (
  input  [7:0] A,
  input  clk,
  input  WE,
  input  OE,
  input  [7:0] D,
  output [7:0] D_out
);

  wire and_1_out, and_2_out, and_3_out, and_4_out, and_5_out, and_6_out, decoder_1_out0, decoder_1_out1,
       decoder_1_out2, decoder_1_out3, decoder_2_out0, decoder_2_out1, decoder_2_out2, decoder_2_out3,
       not_1_out, not_2_out;
  wire [7:0] cell_memo_1_dt_out, cell_memo_5_dt_out, cell_memo_9_dt_out, cell_memo_13_dt_out,
       controlled_buffer_1_out, controlled_buffer_2_out, controlled_buffer_4_out, controlled_buffer_6_out,
       controlled_buffer_8_out;

  Decoder #(.enable("false"), .select(4)) decoder_1 (
    .out0(decoder_1_out0), .out1(decoder_1_out1), .out2(decoder_1_out2), .out3(decoder_1_out3), .sel(A[7:4]));  // open: out4, out5, out6, out7, out8, out9, out10, out11, out12, out13, out14, out15
  and and_1 (and_1_out, WE, clk);
  and and_2 (and_2_out, clk, OE);
  not not_1 (not_1_out, and_2_out);
  assign controlled_buffer_1_out = not_2_out ? controlled_buffer_2_out : 8'bz;  // Controlled_Buffer controlled_buffer_1
  not not_2 (not_2_out, OE);
  assign controlled_buffer_2_out = not_2_out ? D : 8'bz;  // Controlled_Buffer controlled_buffer_2
  cell_memo cell_memo_1 (
    .dt_in(controlled_buffer_1_out), .y(decoder_2_out0), .set(and_1_out), .clk(clk), .x(decoder_1_out0),
    .dt_out(cell_memo_1_dt_out));
  cell_memo cell_memo_2 (
    .dt_in(controlled_buffer_1_out), .y(decoder_2_out0), .set(and_1_out), .clk(clk), .x(decoder_1_out1),
    .dt_out(cell_memo_1_dt_out));
  cell_memo cell_memo_3 (
    .dt_in(controlled_buffer_1_out), .y(decoder_2_out0), .set(and_1_out), .clk(clk), .x(decoder_1_out2),
    .dt_out(cell_memo_1_dt_out));
  cell_memo cell_memo_4 (
    .dt_in(controlled_buffer_1_out), .y(decoder_2_out0), .set(and_1_out), .clk(clk), .x(decoder_1_out3),
    .dt_out(cell_memo_1_dt_out));
  and and_3 (and_3_out, OE, decoder_2_out0);
  assign controlled_buffer_2_out = and_3_out ? cell_memo_1_dt_out : 8'bz;  // Controlled_Buffer controlled_buffer_3
  Decoder #(.enable("false"), .select(4)) decoder_2 (
    .out0(decoder_2_out0), .out1(decoder_2_out1), .out2(decoder_2_out2), .out3(decoder_2_out3), .sel(A[3:0]));  // open: out4, out5, out6, out7, out8, out9, out10, out11, out12, out13, out14, out15
  assign controlled_buffer_4_out = not_2_out ? controlled_buffer_2_out : 8'bz;  // Controlled_Buffer controlled_buffer_4
  cell_memo cell_memo_5 (
    .dt_in(controlled_buffer_4_out), .y(decoder_2_out1), .set(and_1_out), .clk(clk), .x(decoder_1_out0),
    .dt_out(cell_memo_5_dt_out));
  cell_memo cell_memo_6 (
    .dt_in(controlled_buffer_4_out), .y(decoder_2_out1), .set(and_1_out), .clk(clk), .x(decoder_1_out1),
    .dt_out(cell_memo_5_dt_out));
  cell_memo cell_memo_7 (
    .dt_in(controlled_buffer_4_out), .y(decoder_2_out1), .set(and_1_out), .clk(clk), .x(decoder_1_out2),
    .dt_out(cell_memo_5_dt_out));
  cell_memo cell_memo_8 (
    .dt_in(controlled_buffer_4_out), .y(decoder_2_out1), .set(and_1_out), .clk(clk), .x(decoder_1_out3),
    .dt_out(cell_memo_5_dt_out));
  and and_4 (and_4_out, OE, decoder_2_out1);
  assign controlled_buffer_2_out = and_4_out ? cell_memo_5_dt_out : 8'bz;  // Controlled_Buffer controlled_buffer_5
  assign controlled_buffer_6_out = not_2_out ? controlled_buffer_2_out : 8'bz;  // Controlled_Buffer controlled_buffer_6
  cell_memo cell_memo_9 (
    .dt_in(controlled_buffer_6_out), .y(decoder_2_out2), .set(and_1_out), .clk(clk), .x(decoder_1_out0),
    .dt_out(cell_memo_9_dt_out));
  cell_memo cell_memo_10 (
    .dt_in(controlled_buffer_6_out), .y(decoder_2_out2), .set(and_1_out), .clk(clk), .x(decoder_1_out1),
    .dt_out(cell_memo_9_dt_out));
  cell_memo cell_memo_11 (
    .dt_in(controlled_buffer_6_out), .y(decoder_2_out2), .set(and_1_out), .clk(clk), .x(decoder_1_out2),
    .dt_out(cell_memo_9_dt_out));
  cell_memo cell_memo_12 (
    .dt_in(controlled_buffer_6_out), .y(decoder_2_out2), .set(and_1_out), .clk(clk), .x(decoder_1_out3),
    .dt_out(cell_memo_9_dt_out));
  and and_5 (and_5_out, OE, decoder_2_out2);
  assign controlled_buffer_2_out = and_5_out ? cell_memo_9_dt_out : 8'bz;  // Controlled_Buffer controlled_buffer_7
  assign controlled_buffer_8_out = not_2_out ? controlled_buffer_2_out : 8'bz;  // Controlled_Buffer controlled_buffer_8
  cell_memo cell_memo_13 (
    .dt_in(controlled_buffer_8_out), .y(decoder_2_out3), .set(and_1_out), .clk(clk), .x(decoder_1_out0),
    .dt_out(cell_memo_13_dt_out));
  cell_memo cell_memo_14 (
    .dt_in(controlled_buffer_8_out), .y(decoder_2_out3), .set(and_1_out), .clk(clk), .x(decoder_1_out1),
    .dt_out(cell_memo_13_dt_out));
  cell_memo cell_memo_15 (
    .dt_in(controlled_buffer_8_out), .y(decoder_2_out3), .set(and_1_out), .clk(clk), .x(decoder_1_out2),
    .dt_out(cell_memo_13_dt_out));
  cell_memo cell_memo_16 (
    .dt_in(controlled_buffer_8_out), .y(decoder_2_out3), .set(and_1_out), .clk(clk), .x(decoder_1_out3),
    .dt_out(cell_memo_13_dt_out));
  and and_6 (and_6_out, OE, decoder_2_out3);
  assign controlled_buffer_2_out = and_6_out ? cell_memo_13_dt_out : 8'bz;  // Controlled_Buffer controlled_buffer_9
  Register register_1 (.D(controlled_buffer_2_out), .Q(D_out), .clk(not_1_out));  // open: en, clr
endmodule

module modelo (
);

  wire undriven, undriven_3, undriven_4, undriven_5, undriven_7, undriven_8, undriven_9, undriven_11,
       undriven_12, undriven_13, undriven_15, undriven_16, undriven_17, undriven_18, undriven_19, undriven_20;
  wire [7:0] cell_memo_1_dt_out, cell_memo_5_dt_out, cell_memo_9_dt_out, cell_memo_13_dt_out, undriven_2,
       undriven_6, undriven_10, undriven_14;

  cell_memo cell_memo_1 (
    .dt_in(undriven_2), .y(undriven), .set(undriven_3), .clk(undriven_4), .x(undriven_17),
    .dt_out(cell_memo_1_dt_out));
  cell_memo cell_memo_2 (
    .dt_in(undriven_2), .y(undriven), .set(undriven_3), .clk(undriven_4), .x(undriven_18),
    .dt_out(cell_memo_1_dt_out));
  cell_memo cell_memo_3 (
    .dt_in(undriven_2), .y(undriven), .set(undriven_3), .clk(undriven_4), .x(undriven_19),
    .dt_out(cell_memo_1_dt_out));
  cell_memo cell_memo_4 (
    .dt_in(undriven_2), .y(undriven), .set(undriven_3), .clk(undriven_4), .x(undriven_20),
    .dt_out(cell_memo_1_dt_out));
  cell_memo cell_memo_5 (
    .dt_in(undriven_6), .y(undriven_5), .set(undriven_7), .clk(undriven_8), .x(undriven_17),
    .dt_out(cell_memo_5_dt_out));
  cell_memo cell_memo_6 (
    .dt_in(undriven_6), .y(undriven_5), .set(undriven_7), .clk(undriven_8), .x(undriven_18),
    .dt_out(cell_memo_5_dt_out));
  cell_memo cell_memo_7 (
    .dt_in(undriven_6), .y(undriven_5), .set(undriven_7), .clk(undriven_8), .x(undriven_19),
    .dt_out(cell_memo_5_dt_out));
  cell_memo cell_memo_8 (
    .dt_in(undriven_6), .y(undriven_5), .set(undriven_7), .clk(undriven_8), .x(undriven_20),
    .dt_out(cell_memo_5_dt_out));
  cell_memo cell_memo_9 (
    .dt_in(undriven_10), .y(undriven_9), .set(undriven_11), .clk(undriven_12), .x(undriven_17),
    .dt_out(cell_memo_9_dt_out));
  cell_memo cell_memo_10 (
    .dt_in(undriven_10), .y(undriven_9), .set(undriven_11), .clk(undriven_12), .x(undriven_18),
    .dt_out(cell_memo_9_dt_out));
  cell_memo cell_memo_11 (
    .dt_in(undriven_10), .y(undriven_9), .set(undriven_11), .clk(undriven_12), .x(undriven_19),
    .dt_out(cell_memo_9_dt_out));
  cell_memo cell_memo_12 (
    .dt_in(undriven_10), .y(undriven_9), .set(undriven_11), .clk(undriven_12), .x(undriven_20),
    .dt_out(cell_memo_9_dt_out));
  cell_memo cell_memo_13 (
    .dt_in(undriven_14), .y(undriven_13), .set(undriven_15), .clk(undriven_16), .x(undriven_17),
    .dt_out(cell_memo_13_dt_out));
  cell_memo cell_memo_14 (
    .dt_in(undriven_14), .y(undriven_13), .set(undriven_15), .clk(undriven_16), .x(undriven_18),
    .dt_out(cell_memo_13_dt_out));
  cell_memo cell_memo_15 (
    .dt_in(undriven_14), .y(undriven_13), .set(undriven_15), .clk(undriven_16), .x(undriven_19),
    .dt_out(cell_memo_13_dt_out));
  cell_memo cell_memo_16 (
    .dt_in(undriven_14), .y(undriven_13), .set(undriven_15), .clk(undriven_16), .x(undriven_20),
    .dt_out(cell_memo_13_dt_out));
endmodule

// sr_l
module shift_l (
  input  carry_in,
  input  [7:0] sinput,
  output [7:0] sout,
  output carry_out
);


  assign carry_out = sinput[7];
  assign sout = {sinput[6:0], carry_in};
endmodule

module ULAT (
  input  carry_in,
  input  [7:0] A,
  input  [7:0] B,
  input  [2:0] func,
  output carry_out,
  output [7:0] sout,
  output zero,
  output a_large,
  output iquals
);

  wire adder_1_cout, or_2_out, shift_l_1_carry_out, shift_r_1_carry_out;
  wire [7:0] adder_1_out, and_1_out, not_1_out, or_1_out, shift_l_1_sout, shift_r_1_sout, xor_1_out;

  Adder adder_1 (.a(A), .b(B), .out(adder_1_out), .cin(carry_in), .cout(adder_1_cout));
  shift_l shift_l_1 (.sinput(A), .carry_in(carry_in), .carry_out(shift_l_1_carry_out), .sout(shift_l_1_sout));
  shift_r shift_r_1 (.sinput(A), .carry_in(carry_in), .carry_out(shift_r_1_carry_out), .sout(shift_r_1_sout));
  assign not_1_out = ~A;  // NOT_Gate not_1, 8 bits wide
  assign and_1_out = A & B;  // AND_Gate and_1, 8 bits wide
  assign or_1_out = A | B;  // OR_Gate or_1, 8 bits wide
  assign xor_1_out = A ^ B;  // XOR_Gate xor_1, 8 bits wide
  Comparator comparator_1 (.a(A), .b(B), .gt(a_large), .eq(iquals));  // open: lt
  Multiplexer #(.select(3), .width(8)) multiplexer_1 (
    .in0(adder_1_out), .in1(shift_l_1_sout), .in2(shift_r_1_sout), .in3(not_1_out), .in4(and_1_out),
    .in5(or_1_out), .in6(xor_1_out), .out(sout), .sel(func));  // open: in7
  Multiplexer #(.select(3)) multiplexer_2 (
    .in0(adder_1_cout), .in1(shift_l_1_carry_out), .in2(shift_r_1_carry_out), .in3(1'b0), .in4(1'b0),
    .in5(1'b0), .in6(1'b0), .in7(1'b0), .out(carry_out), .sel(func));
  or or_2 (or_2_out, sout[0], sout[1], sout[2], sout[3], sout[4], sout[5], sout[6], sout[7]);
  not not_2 (zero, or_2_out);
endmodule

// sr_r
module shift_r (
  input  carry_in,
  input  [7:0] sinput,
  output [7:0] sout,
  output carry_out
);


  assign carry_out = sinput[0];
  assign sout = {carry_in, sinput[7:1]};
endmodule

// reg
module reg2 (
  input  [7:0] in_1,
  input  clk,
  input  buffer_endble,
  output [7:0] out_4
);

  wire [7:0] register_1_q;

  Register register_1 (.D(in_1), .Q(register_1_q), .clk(clk));  // open: en, clr
  assign out_4 = buffer_endble ? register_1_q : 8'bz;  // Controlled_Buffer controlled_buffer_1
endmodule
