// Logisim project Unidade_de_controle.circ as structural Verilog
// cdnaRt
module cmp_dec_nArt (
  input  operacao,
  input  in1,
  input  in2,
  input  in3,
  output p0000,
  output p0001,
  output p0010,
  output p0011,
  output p0100,
  output p0101,
  output p0110,
  output p0111
);

  wire decoder_1_out0, decoder_1_out1, decoder_1_out2, decoder_1_out3, decoder_1_out4, decoder_1_out5,
       decoder_1_out6, decoder_1_out7, not_1_out;

  not not_1 (not_1_out, operacao);
  Decoder #(.enable("false"), .select(3)) decoder_1 (
    .out0(decoder_1_out0), .out1(decoder_1_out1), .out2(decoder_1_out2), .out3(decoder_1_out3),
    .out4(decoder_1_out4), .out5(decoder_1_out5), .out6(decoder_1_out6), .out7(decoder_1_out7),
    .sel({in1, in2, in3}));
  and and_1 (p0000, not_1_out, decoder_1_out0);
  and and_2 (p0001, not_1_out, decoder_1_out1);
  and and_3 (p0010, not_1_out, decoder_1_out2);
  and and_4 (p0011, not_1_out, decoder_1_out3);
  and and_5 (p0100, not_1_out, decoder_1_out4);
  and and_6 (p0101, not_1_out, decoder_1_out5);
  and and_7 (p0110, not_1_out, decoder_1_out6);
  and and_8 (p0111, not_1_out, decoder_1_out7);
endmodule

module CU (
  input  carry_out,
  input  a_large,
  input  equal,
  input  zero,
  input  [7:0] in_5,
  output bus1,
  output IR_S,
  output MARSet,
  output IAR,
  output RAM,
  output ACC,
  output OI_clock_e,
  output rg0,
  output rg1,
  output rg2,
  output rg3
);

  wire and_17_out, and_18_out, and_19_out, and_20_out, and_21_out, c1, c2, c3, c4, c5, c6, c7, c8, c9,
       clk_1_clk_n, clk_ena, clk_set, cmp_dec_nart_1_p0000, cmp_dec_nart_1_p0001, cmp_dec_nart_1_p0010,
       cmp_dec_nart_1_p0011, cmp_dec_nart_1_p0100, cmp_dec_nart_1_p0101, cmp_dec_nart_1_p0110,
       cmp_dec_nart_1_p0111, ir_set_1_clk_sout, not_1_out, not_2_out, or_4_out, or_5_out, or_6_out, or_7_out,
       rgA_sing, rgB_sing, stepper_1_spt8, stp1, stp2, stp3, stp4, stp5, stp6, tun1, tun2, tun3, tun4, tun5,
       tun6, tun7, tun8, tun9, tun10;
  wire [2:0] ALU_S;

  or or_1 (bus1, stp1, c8, c7, c4);
  and and_1 (IAR, clk_ena, or_4_out);
  and and_2 (RAM, clk_ena, or_5_out);
  and and_3 (ACC, clk_ena, or_6_out);
  and and_4 (OI_clock_e, clk_ena, tun8);
  or or_2 (rgB_sing, c1, tun9, c5, c9);
  or or_3 (rgA_sing, c3, c2, tun10);
  or or_4 (or_4_out, stp1, c4, c6, c7);
  or or_5 (or_5_out, stp2, tun1, tun2, tun3, tun4);
  or or_6 (or_6_out, stp3, tun5, tun6, tun7);
  clk clk_1 (.clk_s(clk_set), .clk_n(clk_1_clk_n), .clk_e(clk_ena));
  stepper stepper_1 (
    .clk(clk_1_clk_n), .spt1(stp1), .spt2(stp2), .spt3(stp3), .spt5(stp4), .spt6(stp5), .spt7(stp6),
    .spt8(stepper_1_spt8));
  LED led_1 (.in(stepper_1_spt8));
  e_ra_rb e_ra_rb_1 (
    .r0(rg0), .r1(rg1), .r2(rg2), .r4(rg3), .e(clk_ena), .rb(rgB_sing), .ra(rgA_sing), .in_4(in_5[0]),
    .in_5(in_5[1]), .in_6(in_5[2]), .in_7(in_5[4]));
  and and_5 (ALU_S[0], in_5[4], in_5[7], stp5);
  and and_6 (ALU_S[1], in_5[5], in_5[7], stp5);
  and and_7 (ALU_S[2], in_5[6], in_5[7], stp5);
  IR_SET ir_set_1 (.stp(stp2), .clk_set(clk_set), .clk_sout(ir_set_1_clk_sout), .IR_SET_out(IR_S));
  MAR_SET mar_set_1 (
    .in1(stp1), .in2(c7), .in3(c4), .in4(c2), .in5(c3), .in6(c6), .clk_set(ir_set_1_clk_sout),
    .MAR_SET_out(MARSet));  // open: out_9
  cmp_dec_nArt cmp_dec_nart_1 (
    .operacao(in_5[7]), .in1(in_5[6]), .in2(in_5[5]), .in3(in_5[4]), .p0000(cmp_dec_nart_1_p0000),
    .p0001(cmp_dec_nart_1_p0001), .p0010(cmp_dec_nart_1_p0010), .p0011(cmp_dec_nart_1_p0011),
    .p0100(cmp_dec_nart_1_p0100), .p0101(cmp_dec_nart_1_p0101), .p0110(cmp_dec_nart_1_p0110),
    .p0111(cmp_dec_nart_1_p0111));
  and and_8 (c1, stp4, in_5[7]);
  and and_9 (c2, stp4, cmp_dec_nart_1_p0000);
  and and_10 (c3, stp4, cmp_dec_nart_1_p0001);
  and and_11 (c4, stp4, cmp_dec_nart_1_p0010);
  and and_12 (c5, stp4, cmp_dec_nart_1_p0011);
  and and_13 (c6, stp4, cmp_dec_nart_1_p0100);
  and and_14 (c7, stp4, cmp_dec_nart_1_p0101);
  and and_15 (c8, stp4, cmp_dec_nart_1_p0110);
  and and_16 (c9, stp4, cmp_dec_nart_1_p0111, in_5[3]);
  not not_1 (not_1_out, in_5[3]);
  and and_17 (and_17_out, in_5[3], carry_out);
  and and_18 (and_18_out, in_5[2], a_large);
  and and_19 (and_19_out, in_5[1], equal);
  and and_20 (and_20_out, in_5[0], zero);
  and and_21 (and_21_out, in_5[4], in_5[5], in_5[6]);
  and and_22 (tun10, stp5, in_5[7]);
  and and_23 (tun4, stp5, cmp_dec_nart_1_p0000);
  and and_24 (tun9, stp5, cmp_dec_nart_1_p0001);
  and and_25 (tun8, stp5, not_1_out, cmp_dec_nart_1_p0111);
  not not_2 (not_2_out, and_21_out);
  and and_26 (tun3, stp5, cmp_dec_nart_1_p0010);
  and and_27 (tun2, stp5, cmp_dec_nart_1_p0100);
  and and_28 (tun5, stp5, cmp_dec_nart_1_p0101);
  or or_7 (or_7_out, and_17_out, and_18_out, and_19_out, and_20_out);
  and and_29 (tun7, stp6, in_5[7], not_2_out);
  and and_30 (tun1, stp6, cmp_dec_nart_1_p0101, or_7_out);
  and and_31 (tun6, stp6, cmp_dec_nart_1_p0010);

  // Other names for the same wires on the sheet: IR[7:0] = in_5

  // Notes on the sheet:
  //   regB
  //   regA
  //   ALL Enables
  //   ALL_SET
endmodule

// stp
module stepper (
  input  clk,
  output spt8,
  output spt5,
  output spt6,
  output spt7,
  output spt1,
  output spt2,
  output spt3
);

  wire decoder_1_out7;
  wire [2:0] counter_1_q;

  Counter #(.max('h7), .width(3)) counter_1 (
    .D(counter_1_q), .Q(counter_1_q), .up(1'b1), .clk(clk), .clr(decoder_1_out7));  // open: load, count, carry
  Decoder #(.enable("false"), .select(3)) decoder_1 (
    .out0(spt8), .out1(spt1), .out2(spt2), .out3(spt3), .out4(spt5), .out5(spt6), .out6(spt7),
    .out7(decoder_1_out7), .sel(counter_1_q));
endmodule

module clk (
  output clk_s,
  output clk_n,
  output clk_e
);

  wire clk_d_out;

  Clock #(.highDuration(2), .lowDuration(2)) clock_1 (.out(clk_n));
  Clock #(.highDuration(2), .lowDuration(2), .phaseOffset(3)) clk_d (.out(clk_d_out));
  or or_1 (clk_e, clk_n, clk_d_out);
  and and_1 (clk_s, clk_n, clk_d_out);
endmodule

module e_ra_rb (
  input  e,
  input  rb,
  input  ra,
  input  in_4,
  input  in_5,
  input  in_6,
  input  in_7,
  output r0,
  output r1,
  output r2,
  output r4
);

  wire and_1_out, and_2_out, and_3_out, and_4_out, and_5_out, and_6_out, and_7_out, and_8_out,
       decoder_1_out0, decoder_1_out1, decoder_1_out2, decoder_1_out3, decoder_2_out0, decoder_2_out1,
       decoder_2_out2, decoder_2_out3;

  or or_1 (r0, and_1_out, and_5_out);
  or or_2 (r1, and_2_out, and_6_out);
  or or_3 (r2, and_3_out, and_7_out);
  or or_4 (r4, and_4_out, and_8_out);
  and and_1 (and_1_out, e, rb, decoder_1_out0);
  and and_2 (and_2_out, e, rb, decoder_1_out1);
  and and_3 (and_3_out, e, rb, decoder_1_out2);
  and and_4 (and_4_out, e, rb, decoder_1_out3);
  and and_5 (and_5_out, e, ra, decoder_2_out0);
  and and_6 (and_6_out, e, ra, decoder_2_out1);
  and and_7 (and_7_out, e, ra, decoder_2_out2);
  and and_8 (and_8_out, e, ra, decoder_2_out3);
  Decoder #(.enable("false"), .select(2)) decoder_1 (
    .out0(decoder_1_out0), .out1(decoder_1_out1), .out2(decoder_1_out2), .out3(decoder_1_out3),
    .sel({in_5, in_4}));
  Decoder #(.enable("false"), .select(2)) decoder_2 (
    .out0(decoder_2_out0), .out1(decoder_2_out1), .out2(decoder_2_out2), .out3(decoder_2_out3),
    .sel({in_7, in_6}));
endmodule

module IR_SET (
  input  clk_set,
  input  stp,
  output IR_SET_out,
  output clk_sout
);

  and and_1 (IR_SET_out, clk_set, stp);

  assign clk_sout = clk_set;
endmodule

module MAR_SET (
  input  in1,
  input  in2,
  input  clk_set,
  input  in3,
  input  in4,
  input  in5,
  input  in6,
  output MAR_SET_out,
  output out_9
);

  wire or_1_out;

  or or_1 (or_1_out, in1, in2, in3, in4, in5, in6);
  and and_1 (MAR_SET_out, clk_set, or_1_out);

  assign out_9 = clk_set;
endmodule
