// Logisim project aula01122022.circ as structural Verilog: 14 circuits, main circuit main
module main (
  input  [7:0] in_1
);

  wire cu_1_marset, cu_1_reg1_ena, cu_1_reg1_set, cu_1_reg2_ena, cu_1_reg2_set, cu_1_reg3_ena, cu_1_reg3_set,
       cu_1_reg4_ena, cu_1_reg4_set;
  wire [7:0] controlled_buffer_1_out, register_1_q, register_2_q, register_3_q, register_4_q, register_5_q;

  assign controlled_buffer_1_out = cu_1_reg1_ena ? register_1_q : 8'bz;  // Controlled_Buffer controlled_buffer_1
  Register register_1 (.D(controlled_buffer_1_out), .Q(register_1_q), .clk(cu_1_reg1_set));  // open: en, clr
  assign controlled_buffer_1_out = cu_1_reg2_ena ? register_2_q : 8'bz;  // Controlled_Buffer controlled_buffer_2
  Register register_2 (.D(controlled_buffer_1_out), .Q(register_2_q), .clk(cu_1_reg2_set));  // open: en, clr
  Register register_3 (.D(controlled_buffer_1_out), .Q(register_3_q), .clk(cu_1_reg3_set));  // open: en, clr
  CU cu_1 (
    .REG1_SET(cu_1_reg1_set), .REG1_ENA(cu_1_reg1_ena), .REG2_SET(cu_1_reg2_set), .REG2_ENA(cu_1_reg2_ena),
    .REG3_SET(cu_1_reg3_set), .REG3_ENA(cu_1_reg3_ena), .REG4_SET(cu_1_reg4_set), .REG4_ENA(cu_1_reg4_ena),
    .MARSet(cu_1_marset), .in_5(in_1));  // open: to_ula, from_carry_out, from_larger, from_equal, from_zero, to_flag, to_bus_1, TMP_set, to_ACC_S, to_ACC_En, to_IAR_S, to_IAR_E, IR_SETT, Input_output, data_adress, to_iO_e, to_iO_s, to_ram_e, to_ram_S, is_init
  assign controlled_buffer_1_out = cu_1_reg3_ena ? register_3_q : 8'bz;  // Controlled_Buffer controlled_buffer_3
  assign controlled_buffer_1_out = cu_1_reg4_ena ? register_4_q : 8'bz;  // Controlled_Buffer controlled_buffer_4
  Register register_4 (.D(controlled_buffer_1_out), .Q(register_4_q), .clk(cu_1_reg4_set));  // open: en, clr
  Register register_5 (.D(controlled_buffer_1_out), .Q(register_5_q), .clk(cu_1_marset));  // open: en, clr
  RAM ram_1 (.addr(register_5_q));  // open: we, oe, clk, din, dout
endmodule

// cdnaRt
module cmp_dec_nArt (
  input  operacao,
  input  in1,
  input  in2,
  input  in3,
  output p0000,
  output p0001,
  output p0010,
  output p0011,
  output p0100,
  output p0101,
  output p0110,
  output p0111
);

  wire decoder_1_out0, decoder_1_out1, decoder_1_out2, decoder_1_out3, decoder_1_out4, decoder_1_out5,
       decoder_1_out6, decoder_1_out7, not_1_out;

  not not_1 (not_1_out, operacao);
  Decoder #(.enable("false"), .select(3)) decoder_1 (
    .out0(decoder_1_out0), .out1(decoder_1_out1), .out2(decoder_1_out2), .out3(decoder_1_out3),
    .out4(decoder_1_out4), .out5(decoder_1_out5), .out6(decoder_1_out6), .out7(decoder_1_out7),
    .sel({in1, in2, in3}));
  and and_1 (p0000, not_1_out, decoder_1_out0);
  and and_2 (p0001, not_1_out, decoder_1_out1);
  and and_3 (p0010, not_1_out, decoder_1_out2);
  and and_4 (p0011, not_1_out, decoder_1_out3);
  and and_5 (p0100, not_1_out, decoder_1_out4);
  and and_6 (p0101, not_1_out, decoder_1_out5);
  and and_7 (p0110, not_1_out, decoder_1_out6);
  and and_8 (p0111, not_1_out, decoder_1_out7);
endmodule

// UC
module CU (
  input  from_carry_out,
  input  from_larger,
  input  from_equal,
  input  from_zero,
  input  [7:0] in_5,
  output to_bus_1,
  output TMP_set,
  output REG1_SET,
  output REG1_ENA,
  output REG2_SET,
  output REG2_ENA,
  output REG3_SET,
  output REG3_ENA,
  output REG4_SET,
  output REG4_ENA,
  output MARSet,
  output [2:0] to_ula,
  output to_ram_e,
  output to_ram_S,
  output is_init,
  output to_flag,
  output to_ACC_S,
  output to_ACC_En,
  output to_IAR_S,
  output to_IAR_E,
  output IR_SETT,
  output Input_output,
  output data_adress,
  output to_iO_e,
  output to_iO_s
);

  wire acc_set_1_out_7, and_18_out, and_19_out, and_20_out, and_21_out, and_22_out, c1, c2, c3, c4, c5, c6,
       c7, c8, c9, clk_1_clk_n, clk_ena, clk_set, cmp_dec_nart_1_p0000, cmp_dec_nart_1_p0001,
       cmp_dec_nart_1_p0010, cmp_dec_nart_1_p0011, cmp_dec_nart_1_p0100, cmp_dec_nart_1_p0101,
       cmp_dec_nart_1_p0110, cmp_dec_nart_1_p0111, flags_1_out_5, iar_set_1_out_9, ir_set_1_clk_sout,
       mar_set_1_out_9, not_1_out, not_2_out, or_4_out, or_5_out, or_6_out, or_7_out, or_8_out,
       ramset_1_out_4, rgA_sing, rgB_sing, stp1, stp2, stp3, stp4, stp5, stp6, tmpset_1_out_4, tun1, tun2,
       tun3, tun4, tun5, tun6, tun7, tun8, tun9, tun10;

  or or_1 (to_bus_1, stp1, c8, c7, c4);
  and and_1 (to_IAR_E, clk_ena, or_4_out);
  and and_2 (to_ram_e, clk_ena, or_5_out);
  and and_3 (to_ACC_En, clk_ena, or_6_out);
  and and_4 (to_iO_e, clk_ena, tun8);
  or or_2 (rgB_sing, c1, tun9, c5, c9);
  or or_3 (rgA_sing, c3, c2, tun10);
  or or_4 (or_4_out, stp1, c4, c6, c7);
  or or_5 (or_5_out, stp2, tun1, tun2, tun3, tun4);
  or or_6 (or_6_out, stp3, tun5, tun6, tun7);
  clk clk_1 (.clk_s(clk_set), .clk_n(clk_1_clk_n), .clk_e(clk_ena));
  stepper stepper_1 (
    .clk(clk_1_clk_n), .spt1(stp1), .spt2(stp2), .spt3(stp3), .spt5(stp4), .spt6(stp5), .spt7(stp6),
    .spt8(is_init));
  LED led_1 (.in(is_init));
  e_ra_rb e_ra_rb_1 (
    .r0(REG1_ENA), .r1(REG2_ENA), .r2(REG3_ENA), .r4(REG4_ENA), .e(clk_ena), .rb(rgB_sing), .ra(rgA_sing),
    .in_4(in_5[0]), .in_5(in_5[1]), .in_6(in_5[2]), .in_7(in_5[4]));
  and and_5 (to_ula[0], in_5[4], in_5[7], stp5);
  and and_6 (to_ula[1], in_5[5], in_5[7], stp5);
  and and_7 (to_ula[2], in_5[6], in_5[7], stp5);
  IR_SET ir_set_1 (.stp(stp2), .clk_set(clk_set), .clk_sout(ir_set_1_clk_sout), .IR_SET_out(IR_SETT));
  MAR_SET mar_set_1 (
    .in1(stp1), .in2(c7), .in3(c4), .in4(c2), .in5(c3), .in6(c6), .clk_set(ir_set_1_clk_sout),
    .out_9(mar_set_1_out_9), .MAR_SET_out(MARSet));
  IAR_SET iar_set_1 (
    .in_1(stp3), .in_3(c6), .in_4(tun2), .in_5(tun5), .in_6(tun7), .in_7(tun1), .clk_set(mar_set_1_out_9),
    .out_9(iar_set_1_out_9), .out_8(to_IAR_S));
  ACC_SET acc_set_1 (
    .in_2(stp1), .in_3(c4), .in_4(c7), .in_5(tun10), .in_1(iar_set_1_out_9), .out_7(acc_set_1_out_7),
    .out_6(to_ACC_S));
  RAMSET ramset_1 (.in_2(tun9), .in_1(acc_set_1_out_7), .out_4(ramset_1_out_4), .out_3(to_ram_S));
  TMPSET tmpset_1 (.in_2(c1), .in_1(ramset_1_out_4), .out_4(tmpset_1_out_4), .out_3(TMP_set));
  FLAGS flags_1 (.in_2(c8), .in_3(tun10), .in_1(tmpset_1_out_4), .out_5(flags_1_out_5), .out_4(to_flag));
  and and_8 (to_iO_s, flags_1_out_5, c9);
  cmp_dec_nArt cmp_dec_nart_1 (
    .operacao(in_5[7]), .in1(in_5[6]), .in2(in_5[5]), .in3(in_5[4]), .p0000(cmp_dec_nart_1_p0000),
    .p0001(cmp_dec_nart_1_p0001), .p0010(cmp_dec_nart_1_p0010), .p0011(cmp_dec_nart_1_p0011),
    .p0100(cmp_dec_nart_1_p0100), .p0101(cmp_dec_nart_1_p0101), .p0110(cmp_dec_nart_1_p0110),
    .p0111(cmp_dec_nart_1_p0111));
  and and_9 (c1, stp4, in_5[7]);
  and and_10 (c2, stp4, cmp_dec_nart_1_p0000);
  and and_11 (c3, stp4, cmp_dec_nart_1_p0001);
  and and_12 (c4, stp4, cmp_dec_nart_1_p0010);
  and and_13 (c5, stp4, cmp_dec_nart_1_p0011);
  and and_14 (c6, stp4, cmp_dec_nart_1_p0100);
  and and_15 (c7, stp4, cmp_dec_nart_1_p0101);
  and and_16 (c8, stp4, cmp_dec_nart_1_p0110);
  and and_17 (c9, stp4, cmp_dec_nart_1_p0111, in_5[3]);
  not not_1 (not_1_out, in_5[3]);
  and and_18 (and_18_out, in_5[3], from_carry_out);
  and and_19 (and_19_out, in_5[2], from_larger);
  and and_20 (and_20_out, in_5[1], from_equal);
  and and_21 (and_21_out, in_5[0], from_zero);
  and and_22 (and_22_out, in_5[4], in_5[5], in_5[6]);
  and and_23 (tun10, stp5, in_5[7]);
  and and_24 (tun4, stp5, cmp_dec_nart_1_p0000);
  and and_25 (tun9, stp5, cmp_dec_nart_1_p0001);
  and and_26 (tun8, stp5, not_1_out, cmp_dec_nart_1_p0111);
  not not_2 (not_2_out, and_22_out);
  and and_27 (tun3, stp5, cmp_dec_nart_1_p0010);
  and and_28 (tun2, stp5, cmp_dec_nart_1_p0100);
  and and_29 (tun5, stp5, cmp_dec_nart_1_p0101);
  or or_7 (or_7_out, and_18_out, and_19_out, and_20_out, and_21_out);
  and and_30 (tun7, stp6, in_5[7], not_2_out);
  and and_31 (tun1, stp6, cmp_dec_nart_1_p0101, or_7_out);
  and and_32 (tun6, stp6, cmp_dec_nart_1_p0010);
  or or_8 (or_8_out, tun4, tun7, tun3, tun8);
  DECREGS decregs_1 (
    .in0(in_5[0]), .in1(in_5[1]), .in_1(or_8_out), .in_2(clk_set), .rg1(REG1_SET), .rg2(REG2_SET),
    .rg3(REG3_SET), .eg4(REG4_SET));

  assign data_adress = in_5[2];
  assign Input_output = in_5[4];

  // Other names for the same wires on the sheet: ALU_S[2:0] = to_ula; bus001 = to_bus_1;
  //   fromCarryOut545152 = from_carry_out; fromEqual45465 = from_equal; fromLarger54654 = from_larger;
  //   fromZero45465 = from_zero; IR[7:0] = in_5; data_addrress = in_5[2]; IR_SET = IR_SETT; marSet54415 = MARSet;
  //   reg1_101 = REG1_SET; reg1_56451 = REG1_ENA; reg2_465 = REG2_SET; reg2_56451 = REG2_ENA; reg3_454 = REG3_SET;
  //   reg3_56451 = REG3_ENA; reg4_454 = REG4_SET; reg4_56451 = REG4_ENA; tmp02155 = TMP_set;
  //   to_acc_ena65456 = to_ACC_En; to_acc_set65456 = to_ACC_S; toFlags4564 = to_flag

  // Notes on the sheet:
  //   regB
  //   regA
  //   ALL Enables
  //   ALL_SET
endmodule

// stp
module stepper (
  input  clk,
  output spt8,
  output spt5,
  output spt6,
  output spt7,
  output spt1,
  output spt2,
  output spt3
);

  wire decoder_1_out7;
  wire [2:0] counter_1_q;

  Counter #(.max('h7), .width(3)) counter_1 (
    .D(counter_1_q), .Q(counter_1_q), .up(1'b1), .clk(clk), .clr(decoder_1_out7));  // open: load, count, carry
  Decoder #(.enable("false"), .select(3)) decoder_1 (
    .out0(spt8), .out1(spt1), .out2(spt2), .out3(spt3), .out4(spt5), .out5(spt6), .out6(spt7),
    .out7(decoder_1_out7), .sel(counter_1_q));
endmodule

module clk (
  output clk_s,
  output clk_n,
  output clk_e
);

  wire clk_d_out;

  Clock #(.highDuration(2), .lowDuration(2)) clock_1 (.out(clk_n));
  Clock #(.highDuration(2), .lowDuration(2), .phaseOffset(3)) clk_d (.out(clk_d_out));
  or or_1 (clk_e, clk_n, clk_d_out);
  and and_1 (clk_s, clk_n, clk_d_out);
endmodule

module e_ra_rb (
  input  e,
  input  rb,
  input  ra,
  input  in_4,
  input  in_5,
  input  in_6,
  input  in_7,
  output r0,
  output r1,
  output r2,
  output r4
);

  wire and_1_out, and_2_out, and_3_out, and_4_out, and_5_out, and_6_out, and_7_out, and_8_out,
       decoder_1_out0, decoder_1_out1, decoder_1_out2, decoder_1_out3, decoder_2_out0, decoder_2_out1,
       decoder_2_out2, decoder_2_out3;

  or or_1 (r0, and_1_out, and_5_out);
  or or_2 (r1, and_2_out, and_6_out);
  or or_3 (r2, and_3_out, and_7_out);
  or or_4 (r4, and_4_out, and_8_out);
  and and_1 (and_1_out, e, rb, decoder_1_out0);
  and and_2 (and_2_out, e, rb, decoder_1_out1);
  and and_3 (and_3_out, e, rb, decoder_1_out2);
  and and_4 (and_4_out, e, rb, decoder_1_out3);
  and and_5 (and_5_out, e, ra, decoder_2_out0);
  and and_6 (and_6_out, e, ra, decoder_2_out1);
  and and_7 (and_7_out, e, ra, decoder_2_out2);
  and and_8 (and_8_out, e, ra, decoder_2_out3);
  Decoder #(.enable("false"), .select(2)) decoder_1 (
    .out0(decoder_1_out0), .out1(decoder_1_out1), .out2(decoder_1_out2), .out3(decoder_1_out3),
    .sel({in_5, in_4}));
  Decoder #(.enable("false"), .select(2)) decoder_2 (
    .out0(decoder_2_out0), .out1(decoder_2_out1), .out2(decoder_2_out2), .out3(decoder_2_out3),
    .sel({in_7, in_6}));
endmodule

module IR_SET (
  input  clk_set,
  input  stp,
  output IR_SET_out,
  output clk_sout
);

  and and_1 (IR_SET_out, clk_set, stp);

  assign clk_sout = clk_set;
endmodule

module MAR_SET (
  input  in1,
  input  in2,
  input  clk_set,
  input  in3,
  input  in4,
  input  in5,
  input  in6,
  output MAR_SET_out,
  output out_9
);

  wire or_1_out;

  or or_1 (or_1_out, in1, in2, in3, in4, in5, in6);
  and and_1 (MAR_SET_out, clk_set, or_1_out);

  assign out_9 = clk_set;
endmodule

module IAR_SET (
  input  in_1,
  input  clk_set,
  input  in_3,
  input  in_4,
  input  in_5,
  input  in_6,
  input  in_7,
  output out_8,
  output out_9
);

  wire or_1_out;

  or or_1 (or_1_out, in_1, in_3, in_4, in_5, in_6, in_7);
  and and_1 (out_8, clk_set, or_1_out);

  assign out_9 = clk_set;
endmodule

module ACC_SET (
  input  in_1,
  input  in_2,
  input  in_3,
  input  in_4,
  input  in_5,
  output out_6,
  output out_7
);

  wire or_1_out;

  or or_1 (or_1_out, in_2, in_3, in_4, in_5);
  and and_1 (out_6, in_1, or_1_out);

  assign out_7 = in_1;
endmodule

// ds
module DECREGS (
  input  in_1,
  input  in_2,
  input  in0,
  input  in1,
  output rg1,
  output rg2,
  output rg3,
  output eg4
);

  wire decoder_1_out0, decoder_1_out1, decoder_1_out2, decoder_1_out3;

  Decoder #(.enable("false"), .select(2)) decoder_1 (
    .out0(decoder_1_out0), .out1(decoder_1_out1), .out2(decoder_1_out2), .out3(decoder_1_out3),
    .sel({in1, in0}));
  and and_1 (rg1, decoder_1_out0, in_2, in_1);
  and and_2 (rg2, decoder_1_out1, in_2, in_1);
  and and_3 (rg3, decoder_1_out2, in_2, in_1);
  and and_4 (eg4, decoder_1_out3, in_2, in_1);
endmodule

module RAMSET (
  input  in_1,
  input  in_2,
  output out_3,
  output out_4
);

  and and_1 (out_3, in_1, in_2);

  assign out_4 = in_1;
endmodule

module TMPSET (
  input  in_1,
  input  in_2,
  output out_3,
  output out_4
);

  and and_1 (out_3, in_1, in_2);

  assign out_4 = in_1;
endmodule

module FLAGS (
  input  in_1,
  input  in_2,
  input  in_3,
  output out_4,
  output out_5
);

  wire or_1_out;

  or or_1 (or_1_out, in_2, in_3);
  and and_1 (out_4, in_1, or_1_out);

  assign out_5 = in_1;
endmodule
