// Logisim project processadorV1.circ as structural Verilog: 6 circuits, main circuit main
module main (
);

  wire uc_1_p2, uc_1_p3, uc_1_p4, uc_1_p5, uc_1_p6, uc_1_p7, uc_1_p8, uc_1_p9, uc_1_p10, uc_1_p11, uc_1_p12,
       uc_1_p13;
  wire [2:0] uc_1_p1;
  wire [7:0] ACC_q, alu_1_sout, bus_1_1_out_3, mar_q, r0_q, r1_q, r2_q, r3_q, tmp_q;

  Register tmp (.D(ACC_q), .Q(tmp_q), .clk(uc_1_p3));  // open: en, clr
  bus_1 bus_1_1 (.in_1(tmp_q), .out_3(bus_1_1_out_3), .in_2(uc_1_p2));
  ALU alu_1 (
    .A(ACC_q), .B(bus_1_1_out_3), .sout(alu_1_sout), .func(uc_1_p1));  // open: carry_in, carry_out, zero, a_large, iquals
  Register ACC (.D(alu_1_sout), .Q(ACC_q));  // open: en, clk, clr
  Register r0 (.D(ACC_q), .Q(r0_q), .clk(uc_1_p4));  // open: en, clr
  assign ACC_q = uc_1_p5 ? r0_q : 8'bz;  // Controlled_Buffer controlled_buffer_1
  LED led_1 (.in(uc_1_p13));
  // UC uc_1: pin names not known; wires that end beside it: uc_1_p1, uc_1_p2, uc_1_p3, uc_1_p4, uc_1_p5, uc_1_p6, uc_1_p7, uc_1_p8, uc_1_p9, uc_1_p10, uc_1_p11, uc_1_p12, uc_1_p13, ACC_q
  assign ACC_q = uc_1_p7 ? r1_q : 8'bz;  // Controlled_Buffer controlled_buffer_2
  Register r1 (.D(ACC_q), .Q(r1_q), .clk(uc_1_p6));  // open: en, clr
  assign ACC_q = uc_1_p9 ? r2_q : 8'bz;  // Controlled_Buffer controlled_buffer_3
  Register r2 (.D(ACC_q), .Q(r2_q), .clk(uc_1_p8));  // open: en, clr
  Register r3 (.D(ACC_q), .Q(r3_q), .clk(uc_1_p10));  // open: en, clr
  assign ACC_q = uc_1_p11 ? r3_q : 8'bz;  // Controlled_Buffer controlled_buffer_4
  Register mar (.D(ACC_q), .Q(mar_q), .clk(uc_1_p12));  // open: en, clr
  RAM ram_1 (.addr(mar_q));  // open: we, oe, clk, din, dout
endmodule

module UC (
  input  from_carry_out,
  input  from_larger,
  input  from_equal,
  input  from_zero,
  input  [7:0] in_5,
  output to_bus_1,
  output TMP_set,
  output REG1_SET,
  output REG1_ENA,
  output REG2_SET,
  output REG2_ENA,
  output REG3_SET,
  output REG3_ENA,
  output REG4_SET,
  output REG4_ENA,
  output MARSet,
  output [2:0] to_ula,
  output to_ram_e,
  output to_ram_S,
  output is_init,
  output to_flag,
  output to_ACC_S,
  output to_ACC_En,
  output to_IAR_S,
  output to_IAR_E,
  output IR_SETT,
  output Input_output,
  output data_adress,
  output to_iO_e,
  output to_iO_s
);


  // Other names for the same wires on the sheet: ALU_S[2:0] = to_ula; bus001 = to_bus_1; data_addrress = data_adress;
  //   fromCarryOut545152 = from_carry_out; fromEqual45465 = from_equal; fromLarger54654 = from_larger;
  //   fromZero45465 = from_zero; IR[7:0] = in_5; marSet54415 = MARSet; reg1_101 = REG1_SET; reg1_56451 = REG1_ENA;
  //   reg2_465 = REG2_SET; reg2_56451 = REG2_ENA; reg3_454 = REG3_SET; reg3_56451 = REG3_ENA; reg4_454 = REG4_SET;
  //   reg4_56451 = REG4_ENA; tmp02155 = TMP_set; to_acc_ena65456 = to_ACC_En; to_acc_set65456 = to_ACC_S;
  //   toFlags4564 = to_flag
endmodule

module ALU (
  input  carry_in,
  input  [7:0] A,
  input  [7:0] B,
  input  [2:0] func,
  output carry_out,
  output [7:0] sout,
  output zero,
  output a_large,
  output iquals
);

  wire adder_1_cout, or_2_out, shift_l_1_carry_out, shift_r_1_carry_out;
  wire [7:0] adder_1_out, and_1_out, not_1_out, or_1_out, shift_l_1_sout, shift_r_1_sout, xor_1_out;

  Adder adder_1 (.a(A), .b(B), .out(adder_1_out), .cin(carry_in), .cout(adder_1_cout));
  shift_l shift_l_1 (.sinput(A), .carry_in(carry_in), .carry_out(shift_l_1_carry_out), .sout(shift_l_1_sout));
  shift_r shift_r_1 (.sinput(A), .carry_in(carry_in), .carry_out(shift_r_1_carry_out), .sout(shift_r_1_sout));
  assign not_1_out = ~A;  // NOT_Gate not_1, 8 bits wide
  assign and_1_out = A & B;  // AND_Gate and_1, 8 bits wide
  assign or_1_out = A | B;  // OR_Gate or_1, 8 bits wide
  assign xor_1_out = A ^ B;  // XOR_Gate xor_1, 8 bits wide
  Comparator comparator_1 (.a(A), .b(B), .gt(a_large), .eq(iquals));  // open: lt
  Multiplexer #(.select(3), .width(8)) multiplexer_1 (
    .in0(adder_1_out), .in1(shift_l_1_sout), .in2(shift_r_1_sout), .in3(not_1_out), .in4(and_1_out),
    .in5(or_1_out), .in6(xor_1_out), .out(sout), .sel(func));  // open: in7
  Multiplexer #(.select(3)) multiplexer_2 (
    .in0(adder_1_cout), .in1(shift_l_1_carry_out), .in2(shift_r_1_carry_out), .in3(1'b0), .in4(1'b0),
    .in5(1'b0), .in6(1'b0), .in7(1'b0), .out(carry_out), .sel(func));
  or or_2 (or_2_out, sout[0], sout[1], sout[2], sout[3], sout[4], sout[5], sout[6], sout[7]);
  not not_2 (zero, or_2_out);
endmodule

module shift_r (
  input  carry_in,
  input  [7:0] sinput,
  output [7:0] sout,
  output carry_out
);


  assign carry_out = sinput[0];
  assign sout = {carry_in, sinput[7:1]};
endmodule

module shift_l (
  input  carry_in,
  input  [7:0] sinput,
  output [7:0] sout,
  output carry_out
);


  assign carry_out = sinput[7];
  assign sout = {sinput[6:0], carry_in};
endmodule

// bs1
module bus_1 (
  input  [7:0] in_1,
  input  in_2,
  output [7:0] out_3
);

  Multiplexer #(.width(8)) multiplexer_1 (.in0(in_1), .in1(8'h1), .out(out_3), .sel(in_2));
endmodule
