// Logisim project processadorV11.circ as structural Verilog: 23 circuits, main circuit main
module main (
);

  wire alu_1_a_large, alu_1_carry_out, alu_1_iquals, alu_1_zero, and_1_out, and_2_out, comparator_1_eq,
       flagsregiste_1_out_6, flagsregiste_1_out_7, flagsregiste_1_out_8, flagsregiste_1_out_9, or_1_out,
       register_1_q, register_2_q, toram_1_clk, toram_1_oeram, toram_1_weram, uc_1_data_adress,
       uc_1_input_output, uc_1_ir_sett, uc_1_marset, uc_1_reg1_ena, uc_1_reg1_set, uc_1_reg2_ena,
       uc_1_reg2_set, uc_1_reg3_ena, uc_1_reg3_set, uc_1_reg4_ena, uc_1_reg4_set, uc_1_tmp_set,
       uc_1_to_acc_en, uc_1_to_acc_s, uc_1_to_bus_1, uc_1_to_flag, uc_1_to_iar_e, uc_1_to_iar_s,
       uc_1_to_io_e, uc_1_to_io_s, uc_1_to_ram_e, uc_1_to_ram_s;
  wire [2:0] uc_1_to_ula;
  wire [6:0] keyboard_1_data;
  wire [7:0] ACC_out_4, alu_1_sout, bit_extender_1_out, bus_1_1_out_3, IR_out_3, mar_q, register_3_q,
       registerpeson3_1_out_3;

  // Probe on ACC_out_4
  registerPeson3 registerpeson3_1 (.in_2(ACC_out_4), .S(uc_1_tmp_set), .out_3(registerpeson3_1_out_3));
  bus_1 bus_1_1 (.in_1(registerpeson3_1_out_3), .in_2(uc_1_to_bus_1), .out_3(bus_1_1_out_3));
  ALU alu_1 (
    .func(uc_1_to_ula), .b1(uc_1_to_bus_1), .carry_in(flagsregiste_1_out_6), .A(ACC_out_4),
    .B(bus_1_1_out_3), .sout(alu_1_sout), .carry_out(alu_1_carry_out), .a_large(alu_1_a_large),
    .iquals(alu_1_iquals), .zero(alu_1_zero));
  registerPerson1 ACC (.in_2(alu_1_sout), .E(uc_1_to_acc_en), .S(uc_1_to_acc_s), .out_4(ACC_out_4));
  flagsRegiste flagsregiste_1 (
    .c(alu_1_carry_out), .a(alu_1_a_large), .e(alu_1_iquals), .z(alu_1_zero), .out_6(flagsregiste_1_out_6),
    .out_7(flagsregiste_1_out_7), .out_8(flagsregiste_1_out_8), .out_9(flagsregiste_1_out_9), .s(uc_1_to_flag));
  registersMemo registersmemo_1 (.in_2(ACC_out_4), .S(uc_1_reg1_set), .E(uc_1_reg1_ena), .out_4(ACC_out_4));
  UC uc_1 (
    .in_5(IR_out_3), .from_larger(flagsregiste_1_out_7), .from_equal(flagsregiste_1_out_8),
    .from_zero(flagsregiste_1_out_9), .from_carry_out(flagsregiste_1_out_6), .to_IAR_E(uc_1_to_iar_e),
    .REG2_ENA(uc_1_reg2_ena), .REG3_SET(uc_1_reg3_set), .IR_SETT(uc_1_ir_sett), .REG3_ENA(uc_1_reg3_ena),
    .Input_output(uc_1_input_output), .REG4_SET(uc_1_reg4_set), .REG4_ENA(uc_1_reg4_ena),
    .data_adress(uc_1_data_adress), .MARSet(uc_1_marset), .to_flag(uc_1_to_flag), .to_iO_e(uc_1_to_io_e),
    .to_ula(uc_1_to_ula), .to_iO_s(uc_1_to_io_s), .to_ram_e(uc_1_to_ram_e), .to_ram_S(uc_1_to_ram_s),
    .to_bus_1(uc_1_to_bus_1), .to_ACC_S(uc_1_to_acc_s), .TMP_set(uc_1_tmp_set), .to_ACC_En(uc_1_to_acc_en),
    .REG1_SET(uc_1_reg1_set), .REG1_ENA(uc_1_reg1_ena), .to_IAR_S(uc_1_to_iar_s), .REG2_SET(uc_1_reg2_set));
  registerPerson2 IAR (.in_2(ACC_out_4), .S(uc_1_to_iar_s), .E(uc_1_to_iar_e), .out_4(ACC_out_4));
  registersMemo registersmemo_2 (.in_2(ACC_out_4), .S(uc_1_reg2_set), .E(uc_1_reg2_ena), .out_4(ACC_out_4));
  registersMemo registersmemo_3 (.in_2(ACC_out_4), .S(uc_1_reg3_set), .E(uc_1_reg3_ena), .out_4(ACC_out_4));
  registerInstro IR (.in_2(ACC_out_4), .S(uc_1_ir_sett), .out_3(IR_out_3));
  registersMemo registersmemo_4 (.in_2(ACC_out_4), .S(uc_1_reg4_set), .E(uc_1_reg4_ena), .out_4(ACC_out_4));
  Register mar (.D(ACC_out_4), .Q(mar_q), .clk(uc_1_marset));  // open: en, clr
  toRam toram_1 (
    .toRamE(uc_1_to_ram_e), .toRamS(uc_1_to_ram_s), .weRam(toram_1_weram), .oeRam(toram_1_oeram),
    .clk(toram_1_clk));
  monitor monitor_1 (.i_o(uc_1_to_io_s), .dt_addrs(uc_1_data_adress), .io_s(uc_1_input_output), .barramento(ACC_out_4));
  RAM #(.databus("bidir")) ram_1 (
    .addr(mar_q), .we(toram_1_weram), .oe(toram_1_oeram), .clk(toram_1_clk), .data(ACC_out_4));
  or or_1 (or_1_out, uc_1_input_output, and_2_out);
  and and_1 (and_1_out, uc_1_to_io_s, uc_1_data_adress, uc_1_input_output);
  Register #(.width(1)) register_1 (.D(uc_1_input_output), .Q(register_1_q), .clk(or_1_out));  // open: en, clr
  Comparator comparator_1 (.a(ACC_out_4), .b(8'h81), .eq(comparator_1_eq));  // open: gt, lt
  and and_2 (and_2_out, register_1_q, uc_1_to_io_e);
  Register #(.width(1)) register_2 (.D(comparator_1_eq), .Q(register_2_q), .clk(and_1_out));  // open: en, clr
  Keyboard #(.buflen(8)) keyboard_1 (.clk(and_2_out), .re(register_2_q), .data(keyboard_1_data));  // open: clr, avail
  // Probe on ACC_out_4
  assign bit_extender_1_out = {{1{1'b0}}, keyboard_1_data};  // Bit_Extender bit_extender_1
  assign ACC_out_4 = uc_1_to_io_e ? register_3_q : 8'bz;  // Controlled_Buffer controlled_buffer_1
  Register register_3 (.D(bit_extender_1_out), .Q(register_3_q), .clk(uc_1_to_io_e));  // open: en, clr

  // Notes on the sheet:
  //   MAT: 22152258
  //   Natanael Bezerra de Oliveira
endmodule

module UC (
  input  from_carry_out,
  input  from_larger,
  input  from_equal,
  input  from_zero,
  input  [7:0] in_5,
  output to_bus_1,
  output TMP_set,
  output REG1_SET,
  output REG1_ENA,
  output REG2_SET,
  output REG2_ENA,
  output REG3_SET,
  output REG3_ENA,
  output REG4_SET,
  output REG4_ENA,
  output MARSet,
  output [2:0] to_ula,
  output to_ram_e,
  output to_ram_S,
  output to_flag,
  output to_ACC_S,
  output to_ACC_En,
  output to_IAR_S,
  output to_IAR_E,
  output IR_SETT,
  output Input_output,
  output data_adress,
  output to_iO_e,
  output to_iO_s
);

  wire and_8_out, and_9_out, and_10_out, and_11_out, and_12_out, and_13_out, and_14_out, and_15_out,
       andswithp4_1_p0, andswithp4_1_p1, andswithp4_1_p2, andswithp4_1_p3, andswithp4_1_p4, andswithp4_1_p5,
       andswithp4_1_p6, andswithp4_1_p7, andswithp4_1_p8, andswithp5_1_p0, andswithp5_1_p1, andswithp5_1_p2,
       andswithp5_1_p3, andswithp5_1_p4, andswithp5_1_p5, andswithp5_1_p6, clk_1_clk_e, clk_1_clk_n,
       clk_1_clk_s, cmpnart_1_p0000, cmpnart_1_p0001, cmpnart_1_p0010, cmpnart_1_p0011, cmpnart_1_p0100,
       cmpnart_1_p0101, cmpnart_1_p0110, cmpnart_1_p0111, is_init, not_1_out, not_2_out, or_2_out, or_3_out,
       or_4_out, or_5_out, or_6_out, or_7_out, or_8_out, or_9_out, or_10_out, or_11_out, or_12_out,
       stepper_1_spt1, stepper_1_spt2, stepper_1_spt3, stepper_1_spt4, stepper_1_spt5, stepper_1_spt6;

  clk clk_1 (.clk_s(clk_1_clk_s), .clk_n(clk_1_clk_n), .clk_e(clk_1_clk_e));
  and and_1 (to_IAR_E, clk_1_clk_e, or_2_out);
  and and_2 (to_ram_e, clk_1_clk_e, or_3_out);
  and and_3 (to_ACC_En, clk_1_clk_e, or_4_out);
  and and_4 (to_iO_e, clk_1_clk_e, andswithp5_1_p6);
  and and_5 (to_ula[0], in_5[4], in_5[7], stepper_1_spt5);
  and and_6 (to_ula[1], in_5[5], in_5[7], stepper_1_spt5);
  and and_7 (to_ula[2], in_5[6], in_5[7], stepper_1_spt5);
  or or_1 (to_bus_1, stepper_1_spt1, andswithp4_1_p7, andswithp4_1_p6, andswithp4_1_p3);
  or or_2 (or_2_out, stepper_1_spt1, andswithp4_1_p3, andswithp4_1_p5, andswithp4_1_p6);
  or or_3 (or_3_out, stepper_1_spt2, and_15_out, andswithp5_1_p4, andswithp5_1_p3, andswithp5_1_p1);
  or or_4 (or_4_out, stepper_1_spt3, andswithp5_1_p5, and_14_out, and_13_out);
  or or_5 (or_5_out, andswithp4_1_p0, andswithp5_1_p2, andswithp4_1_p4, andswithp4_1_p8);
  or or_6 (or_6_out, andswithp4_1_p2, andswithp4_1_p1, andswithp5_1_p0);
  e_ra_rb e_ra_rb_1 (
    .r0(REG1_ENA), .r1(REG2_ENA), .r2(REG3_ENA), .r4(REG4_ENA), .e(clk_1_clk_e), .rb(or_5_out),
    .ra(or_6_out), .in_4(in_5[0]), .in_5(in_5[1]), .in_6(in_5[2]), .in_7(in_5[3]));
  LED led_1 (.in(is_init));
  cmpNart cmpnart_1 (
    .operacao(in_5[7]), .in1(in_5[6]), .in2(in_5[5]), .in3(in_5[4]), .p0000(cmpnart_1_p0000),
    .p0001(cmpnart_1_p0001), .p0010(cmpnart_1_p0010), .p0011(cmpnart_1_p0011), .p0100(cmpnart_1_p0100),
    .p0101(cmpnart_1_p0101), .p0110(cmpnart_1_p0110), .p0111(cmpnart_1_p0111));
  stepper stepper_1 (
    .clk(clk_1_clk_n), .spt1(stepper_1_spt1), .spt2(stepper_1_spt2), .spt3(stepper_1_spt3),
    .spt4(stepper_1_spt4), .spt5(stepper_1_spt5), .spt6(stepper_1_spt6), .spt8(is_init));
  andsWithP4 andswithp4_1 (
    .stp4(stepper_1_spt4), .p0(andswithp4_1_p0), .p1(andswithp4_1_p1), .p2(andswithp4_1_p2),
    .p3(andswithp4_1_p3), .p4(andswithp4_1_p4), .p5(andswithp4_1_p5), .p6(andswithp4_1_p6),
    .p7(andswithp4_1_p7), .p8(andswithp4_1_p8), .i0(in_5[7]), .i1(cmpnart_1_p0000), .i2(cmpnart_1_p0001),
    .i3(cmpnart_1_p0010), .i4(cmpnart_1_p0011), .i5(cmpnart_1_p0100), .i6(cmpnart_1_p0101),
    .i7(cmpnart_1_p0110), .i8(cmpnart_1_p0111), .i9(in_5[3]));
  not not_1 (not_1_out, in_5[3]);
  and and_8 (and_8_out, in_5[4], in_5[5], in_5[6]);
  andsWithP5 andswithp5_1 (
    .in_1(stepper_1_spt5), .p0(andswithp5_1_p0), .p1(andswithp5_1_p1), .p2(andswithp5_1_p2),
    .p3(andswithp5_1_p3), .p4(andswithp5_1_p4), .p5(andswithp5_1_p5), .p6(andswithp5_1_p6), .o0(in_5[7]),
    .o1(cmpnart_1_p0000), .o2(cmpnart_1_p0001), .o3(cmpnart_1_p0010), .o4(cmpnart_1_p0100),
    .o5(cmpnart_1_p0101), .o6(cmpnart_1_p0111), .o7(not_1_out));
  and and_9 (and_9_out, in_5[3], from_carry_out);
  and and_10 (and_10_out, in_5[2], from_larger);
  and and_11 (and_11_out, in_5[1], from_equal);
  and and_12 (and_12_out, in_5[0], from_zero);
  not not_2 (not_2_out, and_8_out);
  or or_7 (or_7_out, and_9_out, and_10_out, and_11_out, and_12_out);
  and and_13 (and_13_out, stepper_1_spt6, not_2_out, in_5[7]);
  and and_14 (and_14_out, stepper_1_spt6, cmpnart_1_p0010);
  and and_15 (and_15_out, stepper_1_spt6, cmpnart_1_p0101, or_7_out);
  or or_8 (or_8_out, andswithp5_1_p1, and_13_out, andswithp5_1_p3, andswithp5_1_p6);
  or or_9 (or_9_out, stepper_1_spt1, andswithp4_1_p3, andswithp4_1_p6, andswithp4_1_p1, andswithp4_1_p2, andswithp4_1_p5);
  or or_10 (or_10_out, stepper_1_spt3, andswithp4_1_p4, andswithp5_1_p4, andswithp5_1_p5, and_14_out, and_15_out);
  or or_11 (or_11_out, stepper_1_spt1, andswithp4_1_p3, andswithp4_1_p6, andswithp5_1_p0);
  or or_12 (or_12_out, andswithp4_1_p7, andswithp5_1_p0);
  and and_16 (IR_SETT, clk_1_clk_s, stepper_1_spt2);
  and and_17 (MARSet, clk_1_clk_s, or_9_out);
  and and_18 (to_IAR_S, clk_1_clk_s, or_10_out);
  and and_19 (to_ACC_S, clk_1_clk_s, or_11_out);
  and and_20 (to_ram_S, clk_1_clk_s, andswithp5_1_p2);
  and and_21 (TMP_set, clk_1_clk_s, andswithp4_1_p0);
  and and_22 (to_flag, clk_1_clk_s, or_12_out);
  decRegs decregs_1 (
    .in0(in_5[0]), .in1(in_5[1]), .in_1(or_8_out), .in_2(clk_1_clk_s), .rg1(REG1_SET), .rg2(REG2_SET),
    .rg3(REG3_SET), .eg4(REG4_SET));
  and and_23 (to_iO_s, clk_1_clk_s, andswithp4_1_p8);

  assign data_adress = in_5[2];
  assign Input_output = in_5[3];

  // Other names for the same wires on the sheet: ALU_S[2:0] = to_ula; bus001 = to_bus_1;
  //   fromCarryOut545152 = from_carry_out; fromEqual45465 = from_equal; fromLarger54654 = from_larger;
  //   fromZero45465 = from_zero; IR[7:0] = in_5; data_addrress = in_5[2]; marSet54415 = MARSet; reg1_101 = REG1_SET;
  //   reg1_56451 = REG1_ENA; reg2_465 = REG2_SET; reg2_56451 = REG2_ENA; reg3_454 = REG3_SET; reg3_56451 = REG3_ENA;
  //   reg4_454 = REG4_SET; reg4_56451 = REG4_ENA; tmp02155 = TMP_set; to_acc_ena65456 = to_ACC_En;
  //   to_acc_set65456 = to_ACC_S; toFlags4564 = to_flag
endmodule

module ALU (
  input  [2:0] func,
  input  b1,
  input  carry_in,
  input  [7:0] A,
  input  [7:0] B,
  output carry_out,
  output a_large,
  output iquals,
  output zero,
  output [7:0] sout
);

  wire adder_1_cout, and_2_out, carry_in_t, not_2_out, or_2_out, shift_l_1_carry_out, shift_r_1_carry_out;
  wire [7:0] adder_1_out, and_1_out, not_1_out, or_1_out, shift_l_1_sout, shift_r_1_sout, xor_1_out;

  Adder adder_1 (.a(A), .b(B), .out(adder_1_out), .cin(carry_in_t), .cout(adder_1_cout));
  shift_r shift_r_1 (.sinput(A), .carry_in(carry_in_t), .carry_out(shift_r_1_carry_out), .sout(shift_r_1_sout));
  shift_l shift_l_1 (.sinput(A), .carry_in(carry_in_t), .carry_out(shift_l_1_carry_out), .sout(shift_l_1_sout));
  assign not_1_out = ~A;  // NOT_Gate not_1, 8 bits wide
  assign and_1_out = A & B;  // AND_Gate and_1, 8 bits wide
  assign or_1_out = A | B;  // OR_Gate or_1, 8 bits wide
  assign xor_1_out = A ^ B;  // XOR_Gate xor_1, 8 bits wide
  Comparator comparator_1 (.a(A), .b(B), .gt(a_large), .eq(iquals));  // open: lt
  Multiplexer #(.select(3), .width(8)) multiplexer_1 (
    .in0(adder_1_out), .in1(shift_r_1_sout), .in2(shift_l_1_sout), .in3(not_1_out), .in4(and_1_out),
    .in5(or_1_out), .in6(xor_1_out), .out(sout), .sel(func));  // open: in7
  and and_2 (and_2_out, func[0], func[1], func[2]);
  Multiplexer #(.select(3)) multiplexer_2 (
    .in0(adder_1_cout), .in1(shift_r_1_carry_out), .in2(shift_l_1_carry_out), .in3(1'b0), .in4(1'b0),
    .in5(1'b0), .in6(1'b0), .in7(1'b0), .out(carry_out), .sel(func));
  or or_2 (or_2_out, sout[0], sout[1], sout[2], sout[3], sout[4], sout[5], sout[6], sout[7]);
  and and_3 (carry_in_t, ~b1, carry_in);  // AND_Gate
  not not_2 (not_2_out, or_2_out);
  Multiplexer multiplexer_3 (.in0(not_2_out), .in1(1'b0), .out(zero), .sel(and_2_out));

  // Other names for the same wires on the sheet: equals = iquals; funct[2:0] = func; zerooss = zero
endmodule

// r
module shift_r (
  input  carry_in,
  input  [7:0] sinput,
  output [7:0] sout,
  output carry_out
);


  assign carry_out = sinput[0];
  assign sout = {carry_in, sinput[7:1]};
endmodule

// l
module shift_l (
  input  carry_in,
  input  [7:0] sinput,
  output [7:0] sout,
  output carry_out
);


  assign carry_out = sinput[7];
  assign sout = {sinput[6:0], carry_in};
endmodule

// bs1
module bus_1 (
  input  [7:0] in_1,
  input  in_2,
  output [7:0] out_3
);

  Multiplexer #(.width(8)) multiplexer_1 (.in0(in_1), .in1(8'h1), .out(out_3), .sel(in_2));
endmodule

module registerPerson1 (
  input  S,
  input  [7:0] in_2,
  input  E,
  output [7:0] out_4
);

  wire [7:0] ACC_q;

  Register ACC (.D(in_2), .Q(ACC_q), .clk(S));  // open: en, clr
  assign out_4 = E ? ACC_q : 8'bz;  // Controlled_Buffer controlled_buffer_1
endmodule

module registerPerson2 (
  input  S,
  input  [7:0] in_2,
  input  E,
  output [7:0] out_4
);

  wire [7:0] register_1_q;

  Register register_1 (.D(in_2), .Q(register_1_q), .clk(S));  // open: en, clr
  assign out_4 = E ? register_1_q : 8'bz;  // Controlled_Buffer controlled_buffer_1
endmodule

module registerPeson3 (
  input  S,
  input  [7:0] in_2,
  output [7:0] out_3
);

  Register register_1 (.D(in_2), .Q(out_3), .clk(S));  // open: en, clr
endmodule

module clk (
  output clk_s,
  output clk_n,
  output clk_e
);

  wire clk_d_out;

  Clock #(.highDuration(2), .lowDuration(2)) clock_1 (.out(clk_n));
  Clock #(.highDuration(2), .lowDuration(2), .phaseOffset(3)) clk_d (.out(clk_d_out));
  or or_1 (clk_e, clk_n, clk_d_out);
  and and_1 (clk_s, clk_n, clk_d_out);
endmodule

module stepper (
  input  clk,
  output spt8,
  output spt5,
  output spt6,
  output spt4,
  output spt1,
  output spt2,
  output spt3
);

  wire decoder_1_out7;
  wire [2:0] counter_1_q;

  Counter #(.max('h7), .width(3)) counter_1 (
    .D(counter_1_q), .Q(counter_1_q), .up(1'b1), .clk(clk), .clr(decoder_1_out7));  // open: load, count, carry
  Decoder #(.enable("false"), .select(3)) decoder_1 (
    .out0(spt8), .out1(spt1), .out2(spt2), .out3(spt3), .out4(spt4), .out5(spt5), .out6(spt6),
    .out7(decoder_1_out7), .sel(counter_1_q));
endmodule

// cmnArt
module cmpNart (
  input  operacao,
  input  in1,
  input  in2,
  input  in3,
  output p0000,
  output p0001,
  output p0010,
  output p0011,
  output p0100,
  output p0101,
  output p0110,
  output p0111
);

  wire decoder_1_out0, decoder_1_out1, decoder_1_out2, decoder_1_out3, decoder_1_out4, decoder_1_out5,
       decoder_1_out6, decoder_1_out7, not_1_out;

  not not_1 (not_1_out, operacao);
  Decoder #(.enable("false"), .select(3)) decoder_1 (
    .out0(decoder_1_out0), .out1(decoder_1_out1), .out2(decoder_1_out2), .out3(decoder_1_out3),
    .out4(decoder_1_out4), .out5(decoder_1_out5), .out6(decoder_1_out6), .out7(decoder_1_out7),
    .sel({in1, in2, in3}));
  and and_1 (p0000, not_1_out, decoder_1_out0);
  and and_2 (p0001, not_1_out, decoder_1_out1);
  and and_3 (p0010, not_1_out, decoder_1_out2);
  and and_4 (p0011, not_1_out, decoder_1_out3);
  and and_5 (p0100, not_1_out, decoder_1_out4);
  and and_6 (p0101, not_1_out, decoder_1_out5);
  and and_7 (p0110, not_1_out, decoder_1_out6);
  and and_8 (p0111, not_1_out, decoder_1_out7);
endmodule

module andsWithP4 (
  input  stp4,
  input  i0,
  input  i1,
  input  i2,
  input  i3,
  input  i4,
  input  i5,
  input  i6,
  input  i7,
  input  i8,
  input  i9,
  output p0,
  output p1,
  output p2,
  output p3,
  output p4,
  output p5,
  output p6,
  output p7,
  output p8
);

  and and_1 (p0, i0, stp4);
  and and_2 (p1, i1, stp4);
  and and_3 (p2, i2, stp4);
  and and_4 (p3, i3, stp4);
  and and_5 (p4, i4, stp4);
  and and_6 (p5, i5, stp4);
  and and_7 (p6, i6, stp4);
  and and_8 (p7, i7, stp4);
  and and_9 (p8, stp4, i8, i9);
endmodule

module andsWithP5 (
  input  in_1,
  input  o0,
  input  o1,
  input  o2,
  input  o3,
  input  o4,
  input  o5,
  input  o6,
  input  o7,
  output p0,
  output p1,
  output p2,
  output p3,
  output p4,
  output p5,
  output p6
);

  and and_1 (p0, o0, in_1);
  and and_2 (p1, o1, in_1);
  and and_3 (p2, o2, in_1);
  and and_4 (p3, o3, in_1);
  and and_5 (p4, o4, in_1);
  and and_6 (p5, o5, in_1);
  and and_7 (p6, o6, o7, in_1);
endmodule

module e_ra_rb (
  input  e,
  input  rb,
  input  ra,
  input  in_4,
  input  in_5,
  input  in_6,
  input  in_7,
  output r0,
  output r1,
  output r2,
  output r4
);

  wire and_1_out, and_2_out, and_3_out, and_4_out, and_5_out, and_6_out, and_7_out, and_8_out,
       decoder_1_out0, decoder_1_out1, decoder_1_out2, decoder_1_out3, decoder_2_out0, decoder_2_out1,
       decoder_2_out2, decoder_2_out3;

  or or_1 (r0, and_1_out, and_5_out);
  or or_2 (r1, and_2_out, and_6_out);
  or or_3 (r2, and_3_out, and_7_out);
  or or_4 (r4, and_4_out, and_8_out);
  and and_1 (and_1_out, e, rb, decoder_1_out0);
  and and_2 (and_2_out, e, rb, decoder_1_out1);
  and and_3 (and_3_out, e, rb, decoder_1_out2);
  and and_4 (and_4_out, e, rb, decoder_1_out3);
  and and_5 (and_5_out, e, ra, decoder_2_out0);
  and and_6 (and_6_out, e, ra, decoder_2_out1);
  and and_7 (and_7_out, e, ra, decoder_2_out2);
  and and_8 (and_8_out, e, ra, decoder_2_out3);
  Decoder #(.enable("false"), .select(2)) decoder_1 (
    .out0(decoder_1_out0), .out1(decoder_1_out1), .out2(decoder_1_out2), .out3(decoder_1_out3),
    .sel({in_5, in_4}));
  Decoder #(.enable("false"), .select(2)) decoder_2 (
    .out0(decoder_2_out0), .out1(decoder_2_out1), .out2(decoder_2_out2), .out3(decoder_2_out3),
    .sel({in_7, in_6}));
endmodule

module decRegs (
  input  in_1,
  input  in_2,
  input  in0,
  input  in1,
  output rg1,
  output rg2,
  output rg3,
  output eg4
);

  wire decoder_1_out0, decoder_1_out1, decoder_1_out2, decoder_1_out3;

  Decoder #(.enable("false"), .select(2)) decoder_1 (
    .out0(decoder_1_out0), .out1(decoder_1_out1), .out2(decoder_1_out2), .out3(decoder_1_out3),
    .sel({in1, in0}));
  and and_1 (rg1, decoder_1_out0, in_2, in_1);
  and and_2 (rg2, decoder_1_out1, in_2, in_1);
  and and_3 (rg3, decoder_1_out2, in_2, in_1);
  and and_4 (eg4, decoder_1_out3, in_2, in_1);
endmodule

// flgs
module flagsRegiste (
  input  c,
  input  a,
  input  e,
  input  z,
  input  s,
  output out_6,
  output out_7,
  output out_8,
  output out_9
);

  Register #(.width(4)) register_1 (.D({z, e, a, c}), .Q({out_9, out_8, out_7, out_6}), .clk(s));  // open: en, clr
endmodule

module teste (
  input  [7:0] in_1
);

  wire uc_1_p1, uc_1_p2, uc_1_p3, uc_1_p4, uc_1_p5, uc_1_p6, uc_1_p7, uc_1_p8, undriven, undriven_2,
       undriven_3, undriven_4, undriven_5, undriven_6, undriven_7, undriven_8, undriven_9, undriven_10,
       undriven_11, undriven_12, undriven_13, undriven_14;

  LED led_1 (.in(undriven_5));
  LED led_2 (.in(undriven_7));
  LED led_3 (.in(undriven_8));
  LED led_4 (.in(undriven_9));
  LED led_5 (.in(undriven_2));
  LED led_6 (.in(undriven_3));
  LED led_7 (.in(undriven_4));
  LED led_8 (.in(undriven));
  LED led_9 (.in(undriven_6));
  LED led_10 (.in(undriven_10));
  LED led_11 (.in(undriven_11));
  LED led_12 (.in(undriven_13));
  LED led_13 (.in(undriven_14));
  // UC uc_1: pin names not known; wires that end beside it: uc_1_p1, uc_1_p2, uc_1_p3, uc_1_p4, uc_1_p5, uc_1_p6, uc_1_p7, uc_1_p8, uc_1_p8, uc_1_p8, uc_1_p8, uc_1_p8
  LED led_14 (.in(uc_1_p3));
  LED led_15 (.in(uc_1_p2));
  LED led_16 (.in(undriven_12));
  LED led_17 (.in(uc_1_p1));
  LED led_18 (.in(uc_1_p8));
  LED led_19 (.in(uc_1_p5));
  LED led_20 (.in(uc_1_p6));
  LED led_21 (.in(uc_1_p7));
  LED led_22 (.in(uc_1_p4));
endmodule

module monitor (
  input  [7:0] barramento,
  input  i_o,
  input  dt_addrs,
  input  io_s
);

  wire and_1_out, and_2_out, comparator_1_eq, register_1_q;

  and and_1 (and_1_out, i_o, dt_addrs, io_s);
  and and_2 (and_2_out, i_o, ~dt_addrs, io_s);  // AND_Gate
  Comparator comparator_1 (.a(barramento), .b(8'h80), .eq(comparator_1_eq));  // open: gt, lt
  Register #(.width(1)) register_1 (.D(comparator_1_eq), .Q(register_1_q), .clk(and_1_out));  // open: en, clr
  TTY #(.cols(34)) tty_1 (.data(barramento[6:0]), .clk(and_2_out), .we(register_1_q));  // open: clr
  LED led_1 (.in(register_1_q));
endmodule

module registersMemo (
  input  S,
  input  [7:0] in_2,
  input  E,
  output [7:0] out_4
);

  wire [7:0] register_1_q;

  Register register_1 (.D(in_2), .Q(register_1_q), .clk(S));  // open: en, clr
  assign out_4 = E ? register_1_q : 8'bz;  // Controlled_Buffer controlled_buffer_1
endmodule

module keyBoardControl (
  input  [7:0] barra,
  input  io_s,
  input  io_e,
  input  addr,
  input  iORo,
  input  bufferSing,
  input  [6:0] dataAssi,
  output read,
  output enable,
  output clear,
  output [7:0] outData
);

  wire and_1_out, comparator_1_eq, or_1_out, register_1_q;
  wire [7:0] bit_extender_1_out, register_3_q;

  Register #(.width(1)) register_1 (.D(iORo), .Q(register_1_q), .clk(or_1_out));  // open: en, clr
  or or_1 (or_1_out, iORo, enable);
  and and_1 (and_1_out, io_s, addr, iORo);
  Comparator comparator_1 (.a(barra), .b(8'h81), .eq(comparator_1_eq));  // open: gt, lt
  and and_2 (enable, register_1_q, io_e);
  Register #(.width(1)) register_2 (.D(comparator_1_eq), .Q(read), .clk(and_1_out));  // open: en, clr
  assign outData = enable ? register_3_q : 8'bz;  // Controlled_Buffer controlled_buffer_1
  assign bit_extender_1_out = {{1{1'b0}}, dataAssi};  // Bit_Extender bit_extender_1
  Register register_3 (.D(bit_extender_1_out), .Q(register_3_q), .clk(enable));  // open: en, clr
endmodule

module registerInstro (
  input  S,
  input  [7:0] in_2,
  output [7:0] out_3
);

  Register register_1 (.D(in_2), .Q(out_3), .clk(S));  // open: en, clr
endmodule

module toRam (
  input  toRamE,
  input  toRamS,
  output weRam,
  output oeRam,
  output clk
);

  or or_1 (clk, toRamE, toRamS);

  assign oeRam = toRamE;
  assign weRam = toRamS;
endmodule
