// Logisim project projeto01.circ as structural Verilog: 8 circuits, main circuit main
module main (
  input  in_1,
  input  [7:0] in_2,
  input  [7:0] in_3,
  input  [7:0] in_4,
  input  in_5,
  input  in_6,
  input  in_7,
  input  in_8,
  input  [7:0] in_9,
  input  in_10,
  input  in_11,
  input  [7:0] in_12,
  output [7:0] out_13,
  output [7:0] out_14,
  output out_15
);

  wire decoder_1_out0, decoder_1_out1, decoder_2_out0;
  wire [7:0] register_1_q;

  Register register_1 (.D(in_9), .en(in_10), .Q(register_1_q), .clk(in_11));  // open: clr
  Sum8 sum8_1 (.C__In(in_1), .Ent__A(in_2), .Ent__B(in_4), .Soma(out_14), .C__Out(out_15));
  Decoder #(.enable("false"), .select(4)) decoder_1 (
    .out0(decoder_1_out0), .out1(decoder_1_out1), .sel(register_1_q[7:4]));  // open: out2, out3, out4, out5, out6, out7, out8, out9, out10, out11, out12, out13, out14, out15
  Decoder #(.enable("false"), .select(4)) decoder_2 (
    .out0(decoder_2_out0), .sel(register_1_q[3:0]));  // open: out1, out2, out3, out4, out5, out6, out7, out8, out9, out10, out11, out12, out13, out14, out15
  Mem8 mem8_1 (.S(decoder_2_out0), .E(decoder_1_out0));  // open: in_1, in_2, in_3, out_6
  Mem8 mem8_2 (.S(decoder_2_out0), .E(decoder_1_out1));  // open: in_1, in_2, in_3, out_6
  Mem8 mem8_3 (.S(decoder_2_out0), .E(decoder_1_out0));  // open: in_1, in_2, in_3, out_6
  Mem8 mem8_4 ();  // open: in_1, in_2, in_3, S, E, out_6
  Reg8 reg8_1 (.inpt(in_3), .set(in_5), .endble(in_6), .oyt(out_13));
  Reg8 reg8_2 (.inpt(in_3), .set(in_7), .endble(in_8), .oyt(out_13));
endmodule

module Sum1 (
  input  C__In,
  input  Bit_A,
  input  Bit_B,
  output soma,
  output C__Out
);

  wire and_1_out, and_2_out, xor_1_out;

  xor xor_1 (xor_1_out, Bit_A, Bit_B);
  and and_1 (and_1_out, Bit_A, Bit_B);
  and and_2 (and_2_out, xor_1_out, C__In);
  xor xor_2 (soma, xor_1_out, C__In);
  or or_1 (C__Out, and_2_out, and_1_out);

  // Notes on the sheet:
  //   SOMADOR DE 1 BIT
endmodule

// soma
module Sum8 (
  input  C__In,
  input  [7:0] Ent__A,
  input  [7:0] Ent__B,
  output [7:0] Soma,
  output C__Out
);

  wire sum1_1_c__out, sum1_2_c__out, sum1_3_c__out, sum1_4_c__out, sum1_5_c__out, sum1_6_c__out,
       sum1_7_c__out;

  Sum1 sum1_1 (.C__In(C__In), .Bit_A(Ent__A[0]), .Bit_B(Ent__B[0]), .soma(Soma[0]), .C__Out(sum1_1_c__out));
  Sum1 sum1_2 (.C__In(sum1_1_c__out), .Bit_A(Ent__A[1]), .Bit_B(Ent__B[1]), .soma(Soma[1]), .C__Out(sum1_2_c__out));
  Sum1 sum1_3 (.C__In(sum1_2_c__out), .Bit_A(Ent__A[2]), .Bit_B(Ent__B[2]), .soma(Soma[2]), .C__Out(sum1_3_c__out));
  Sum1 sum1_4 (.C__In(sum1_3_c__out), .Bit_A(Ent__A[3]), .Bit_B(Ent__B[3]), .soma(Soma[3]), .C__Out(sum1_4_c__out));
  Sum1 sum1_5 (.C__In(sum1_4_c__out), .Bit_A(Ent__A[4]), .Bit_B(Ent__B[4]), .soma(Soma[4]), .C__Out(sum1_5_c__out));
  Sum1 sum1_6 (.C__In(sum1_5_c__out), .Bit_A(Ent__A[5]), .Bit_B(Ent__B[5]), .soma(Soma[5]), .C__Out(sum1_6_c__out));
  Sum1 sum1_7 (.C__In(sum1_6_c__out), .Bit_A(Ent__A[6]), .Bit_B(Ent__B[6]), .soma(Soma[6]), .C__Out(sum1_7_c__out));
  Sum1 sum1_8 (.C__In(sum1_7_c__out), .Bit_A(Ent__A[7]), .Bit_B(Ent__B[7]), .soma(Soma[7]), .C__Out(C__Out));

  // Notes on the sheet:
  //   SOMADOR DE 8 BITS
endmodule

// 1Bit
module Mem1 (
  input  Input,
  input  Set,
  output out_3
);

  wire nand_1_out, nand_2_out, nand_4_out;

  nand nand_1 (nand_1_out, Input, Set);
  nand nand_2 (nand_2_out, nand_1_out, Set);
  nand nand_3 (out_3, nand_1_out, nand_4_out);
  nand nand_4 (nand_4_out, out_3, nand_2_out);

  // Notes on the sheet:
  //   Enable
endmodule

module Reg8 (
  input  [7:0] inpt,
  input  set,
  input  endble,
  output [7:0] oyt
);

  wire mem1_1_out_3, mem1_2_out_3, mem1_3_out_3, mem1_4_out_3, mem1_5_out_3, mem1_6_out_3, mem1_7_out_3,
       mem1_8_out_3;

  Mem1 mem1_1 (.Input(inpt[0]), .Set(set), .out_3(mem1_1_out_3));
  Mem1 mem1_2 (.Input(inpt[1]), .Set(set), .out_3(mem1_2_out_3));
  Mem1 mem1_3 (.Input(inpt[2]), .Set(set), .out_3(mem1_3_out_3));
  Mem1 mem1_4 (.Input(inpt[3]), .Set(set), .out_3(mem1_4_out_3));
  Mem1 mem1_5 (.Input(inpt[4]), .Set(set), .out_3(mem1_5_out_3));
  Mem1 mem1_6 (.Input(inpt[5]), .Set(set), .out_3(mem1_6_out_3));
  Mem1 mem1_7 (.Input(inpt[6]), .Set(set), .out_3(mem1_7_out_3));
  Mem1 mem1_8 (.Input(inpt[7]), .Set(set), .out_3(mem1_8_out_3));
  and and_1 (oyt[0], endble, mem1_1_out_3);
  and and_2 (oyt[1], endble, mem1_2_out_3);
  and and_3 (oyt[2], endble, mem1_3_out_3);
  and and_4 (oyt[3], endble, mem1_4_out_3);
  and and_5 (oyt[4], endble, mem1_5_out_3);
  and and_6 (oyt[5], endble, mem1_6_out_3);
  and and_7 (oyt[6], endble, mem1_7_out_3);
  and and_8 (oyt[7], endble, mem1_8_out_3);
endmodule

// R
module Rg2 (
  input  [7:0] dt_input,
  input  clk,
  input  enable,
  input  set,
  output [7:0] dt_output
);

  wire [7:0] register_1_q;

  Register register_1 (.D(dt_input), .en(set), .Q(register_1_q), .clk(clk));  // open: clr
  assign dt_output = enable ? register_1_q : 8'bz;  // Controlled_Buffer controlled_buffer_1
endmodule

module RgFire (
  input  [7:0] Data,
  input  clk,
  input  enable,
  input  WE,
  input  [1:0] in_5,
  output [7:0] out_6
);

  wire and_1_out, and_2_out, and_3_out, and_4_out, and_5_out, and_6_out, and_7_out, and_8_out, and_9_out,
       decoder_1_out0, decoder_1_out1, decoder_1_out2, decoder_1_out3, not_1_out;
  wire [7:0] controlled_buffer_1_out, rg2_1_dt_output, rg2_2_dt_output, rg2_3_dt_output, rg2_4_dt_output;

  Decoder #(.select(2)) decoder_1 (
    .out0(decoder_1_out0), .out1(decoder_1_out1), .out2(decoder_1_out2), .out3(decoder_1_out3), .sel(in_5));  // open: en
  assign controlled_buffer_1_out = not_1_out ? Data : 8'bz;  // Controlled_Buffer controlled_buffer_1
  not not_1 (not_1_out, enable);
  Rg2 rg2_1 (
    .dt_input(controlled_buffer_1_out), .set(and_2_out), .clk(clk), .enable(and_1_out),
    .dt_output(rg2_1_dt_output));
  and and_1 (and_1_out, enable, decoder_1_out0);
  and and_2 (and_2_out, decoder_1_out0, WE);
  assign controlled_buffer_1_out = rg2_1_dt_output;  // Buffer buffer_1, 8 bits wide
  and and_3 (and_3_out, decoder_1_out1, WE);
  assign controlled_buffer_1_out = rg2_2_dt_output;  // Buffer buffer_2, 8 bits wide
  Rg2 rg2_2 (
    .dt_input(controlled_buffer_1_out), .set(and_3_out), .clk(clk), .enable(and_4_out),
    .dt_output(rg2_2_dt_output));
  and and_4 (and_4_out, enable, decoder_1_out1);
  Rg2 rg2_3 (
    .dt_input(controlled_buffer_1_out), .set(and_6_out), .clk(clk), .enable(and_5_out),
    .dt_output(rg2_3_dt_output));
  and and_5 (and_5_out, enable, decoder_1_out2);
  and and_6 (and_6_out, decoder_1_out2, WE);
  assign controlled_buffer_1_out = rg2_3_dt_output;  // Buffer buffer_3, 8 bits wide
  and and_7 (and_7_out, decoder_1_out3, WE);
  assign controlled_buffer_1_out = rg2_4_dt_output;  // Buffer buffer_4, 8 bits wide
  Rg2 rg2_4 (
    .dt_input(controlled_buffer_1_out), .set(and_7_out), .clk(clk), .enable(and_8_out),
    .dt_output(rg2_4_dt_output));
  and and_8 (and_8_out, enable, decoder_1_out3);
  Register register_1 (.D(controlled_buffer_1_out), .Q(out_6), .clk(and_9_out));  // open: en, clr
  and and_9 (and_9_out, clk, enable);

  // Notes on the sheet:
  //   AD
endmodule

// Cel
module Mem8 (
  input  [7:0] in_1,
  input  in_2,
  input  in_3,
  input  S,
  input  E,
  output [7:0] out_6
);

  wire and_1_out, and_2_out, and_3_out;

  and and_1 (and_1_out, in_2, in_3);
  and and_2 (and_2_out, and_1_out, S);
  and and_3 (and_3_out, and_1_out, E);
  Reg8 reg8_1 (.inpt(in_1), .set(and_2_out), .endble(and_3_out), .oyt(out_6));

  // Notes on the sheet:
  //   S
  //   E
endmodule
