// Logisim project aula2.circ as structural Verilog
module main (
  input  [7:0] in_1,
  input  in_2,
  input  in_3,
  input  in_4,
  input  in_5,
  output [7:0] out_6
);

  registrador registrador_1 (.in_1(in_1), .in_3(in_2), .in_2(in_3), .out_4(out_6));
  registrador registrador_2 (.in_1(in_1), .in_3(in_4), .in_2(in_5), .out_4(out_6));
endmodule

// R
module registrador (
  input  [7:0] in_1,
  input  in_2,
  input  in_3,
  output [7:0] out_4
);

  wire onebit_1_out_3, onebit_2_out_3, onebit_3_out_3, onebit_4_out_3, onebit_5_out_3, onebit_6_out_3,
       onebit_7_out_3, onebit_8_out_3;

  onebit onebit_1 (.in_1(in_1[0]), .in_2(in_3), .out_3(onebit_1_out_3));
  onebit onebit_2 (.in_1(in_1[1]), .in_2(in_3), .out_3(onebit_2_out_3));
  onebit onebit_3 (.in_1(in_1[2]), .in_2(in_3), .out_3(onebit_3_out_3));
  onebit onebit_4 (.in_1(in_1[3]), .in_2(in_3), .out_3(onebit_4_out_3));
  onebit onebit_5 (.in_1(in_1[4]), .in_2(in_3), .out_3(onebit_5_out_3));
  onebit onebit_6 (.in_1(in_1[5]), .in_2(in_3), .out_3(onebit_6_out_3));
  onebit onebit_7 (.in_1(in_1[6]), .in_2(in_3), .out_3(onebit_7_out_3));
  onebit onebit_8 (.in_1(in_1[7]), .in_2(in_3), .out_3(onebit_8_out_3));
  and and_1 (out_4[0], onebit_1_out_3, in_2);
  and and_2 (out_4[1], onebit_2_out_3, in_2);
  and and_3 (out_4[2], onebit_3_out_3, in_2);
  and and_4 (out_4[3], onebit_4_out_3, in_2);
  and and_5 (out_4[4], onebit_5_out_3, in_2);
  and and_6 (out_4[5], onebit_6_out_3, in_2);
  and and_7 (out_4[6], onebit_7_out_3, in_2);
  and and_8 (out_4[7], onebit_8_out_3, in_2);
endmodule

// 1b
module onebit (
  input  in_1,
  input  in_2,
  output out_3
);

  wire nand_1_out, nand_2_out, nand_4_out;

  nand nand_1 (nand_1_out, in_1, in_2);
  nand nand_2 (nand_2_out, nand_1_out, in_2);
  nand nand_3 (out_3, nand_1_out, nand_4_out);
  nand nand_4 (nand_4_out, out_3, nand_2_out);
endmodule

// R
module registerFile (
);

  wire [7:0] registrador_1_out_4;

  // AND_Gate and_1 is placed but not wired
  // AND_Gate and_2 is placed but not wired
  // AND_Gate and_3 is placed but not wired
  // AND_Gate and_4 is placed but not wired
  // AND_Gate and_5 is placed but not wired
  // AND_Gate and_6 is placed but not wired
  // AND_Gate and_7 is placed but not wired
  registrador registrador_1 (.out_4(registrador_1_out_4));  // open: in_1, in_3, in_2
  registrador registrador_2 (.out_4(registrador_1_out_4));  // open: in_1, in_3, in_2
  registrador registrador_3 (.out_4(registrador_1_out_4));  // open: in_1, in_3, in_2
  registrador registrador_4 (.out_4(registrador_1_out_4));  // open: in_1, in_3, in_2
endmodule

module R (
  input  [7:0] in_1,
  input  S,
  input  E,
  output [7:0] out_4
);

  wire [7:0] register_1_q;

  Register register_1 (.D(in_1), .Q(register_1_q), .clk(S));  // open: en, clr
  assign out_4 = E ? register_1_q : 8'bz;  // Controlled_Buffer controlled_buffer_1

  // Notes on the sheet:
  //   Aula 03/11
endmodule

module mainR (
  input  [7:0] D,
  input  WE,
  input  [1:0] A
);

  wire and_1_out, and_2_out, and_3_out, and_4_out, decoder_1_out0, decoder_1_out1, decoder_1_out2,
       decoder_1_out3;

  Decoder #(.select(2)) decoder_1 (
    .out0(decoder_1_out0), .out1(decoder_1_out1), .out2(decoder_1_out2), .out3(decoder_1_out3), .sel(A));  // open: en
  R r_1 (.in_1(D), .S(and_1_out), .out_4(D));  // open: E
  and and_1 (and_1_out, decoder_1_out0, WE);
  R r_2 (.in_1(D), .S(and_2_out), .out_4(D));  // open: E
  and and_2 (and_2_out, decoder_1_out1, WE);
  R r_3 (.in_1(D), .S(and_3_out), .out_4(D));  // open: E
  and and_3 (and_3_out, decoder_1_out2, WE);
  R r_4 (.in_1(D), .S(and_4_out), .out_4(D));  // open: E
  and and_4 (and_4_out, decoder_1_out3, WE);

  // Notes on the sheet:
  //   write enable
  //   dado
  //   endereço
endmodule

module memory (
  input  [7:0] in_1,
  input  in_2
);

  wire decoder_1_out0, decoder_1_out1, decoder_1_out2, decoder_1_out3, decoder_1_out4, decoder_1_out5,
       decoder_1_out6, decoder_1_out7, decoder_1_out8, decoder_1_out9, decoder_1_out10, decoder_1_out11,
       decoder_1_out12, decoder_1_out13, decoder_1_out14, decoder_1_out15, decoder_2_out0, decoder_2_out1,
       decoder_2_out2, decoder_2_out3, decoder_2_out4, decoder_2_out5, decoder_2_out6, decoder_2_out7,
       decoder_2_out8, decoder_2_out9, decoder_2_out10, decoder_2_out11, decoder_2_out12, decoder_2_out13,
       decoder_2_out14, decoder_2_out15;
  wire [7:0] register_1_q;

  Register register_1 (.D(in_1), .Q(register_1_q), .clk(in_2));  // open: en, clr
  Decoder #(.enable("false"), .select(4)) decoder_1 (
    .out0(decoder_1_out0), .out1(decoder_1_out1), .out2(decoder_1_out2), .out3(decoder_1_out3),
    .out4(decoder_1_out4), .out5(decoder_1_out5), .out6(decoder_1_out6), .out7(decoder_1_out7),
    .out8(decoder_1_out8), .out9(decoder_1_out9), .out10(decoder_1_out10), .out11(decoder_1_out11),
    .out12(decoder_1_out12), .out13(decoder_1_out13), .out14(decoder_1_out14), .out15(decoder_1_out15),
    .sel(register_1_q[7:4]));
  Decoder #(.enable("false"), .select(4)) decoder_2 (
    .out0(decoder_2_out0), .out1(decoder_2_out1), .out2(decoder_2_out2), .out3(decoder_2_out3),
    .out4(decoder_2_out4), .out5(decoder_2_out5), .out6(decoder_2_out6), .out7(decoder_2_out7),
    .out8(decoder_2_out8), .out9(decoder_2_out9), .out10(decoder_2_out10), .out11(decoder_2_out11),
    .out12(decoder_2_out12), .out13(decoder_2_out13), .out14(decoder_2_out14), .out15(decoder_2_out15),
    .sel(register_1_q[3:0]));
  // AND_Gate and_1 has open pins: in0=decoder_1_out0, in1=decoder_2_out0, out=open
  // AND_Gate and_2 has open pins: in0=decoder_1_out1, in1=decoder_2_out1, out=open
  // AND_Gate and_3 has open pins: in0=decoder_1_out2, in1=decoder_2_out2, out=open
  // AND_Gate and_4 has open pins: in0=decoder_1_out3, in1=decoder_2_out3, out=open
  // AND_Gate and_5 has open pins: in0=decoder_1_out4, in1=decoder_2_out4, out=open
endmodule
