// Logisim project memo.circ as structural Verilog: 11 circuits, main circuit main
module main (
  input  [7:0] in_1,
  input  we,
  input  oe,
  input  clk,
  input  [7:0] in_5,
  output [7:0] out_6,
  output [7:0] out_7,
  output [7:0] out_8
);

  RAM ram_1 (.addr(in_1), .we(we), .oe(oe), .clk(clk), .din(in_5), .dout(out_6));
  ram_t ram_t_1 (.A(in_1), .clk(clk), .WE(we), .D(in_5), .OE(oe), .out_6(out_7));
  memo_test memo_test_1 (.A(in_1), .clk(clk), .WE(we), .D(in_5), .OE(oe), .out_6(out_8));
endmodule

module registrador (
  input  [7:0] inp,
  input  enble,
  input  clk,
  output [7:0] s_out
);

  wire multiplexer_1_out, multiplexer_2_out, multiplexer_3_out, multiplexer_4_out, multiplexer_5_out,
       multiplexer_6_out, multiplexer_7_out, multiplexer_8_out;

  Multiplexer multiplexer_1 (.in0(s_out[0]), .in1(inp[0]), .out(multiplexer_1_out), .sel(enble));
  D_Flip_Flop d_ff_1 (.D(multiplexer_1_out), .clk(clk), .Q(s_out[0]));  // open: Qn, preset, reset
  D_Flip_Flop d_ff_2 (.D(multiplexer_2_out), .clk(clk), .Q(s_out[1]));  // open: Qn, preset, reset
  Multiplexer multiplexer_2 (.in0(s_out[1]), .in1(inp[1]), .out(multiplexer_2_out), .sel(enble));
  D_Flip_Flop d_ff_3 (.D(multiplexer_3_out), .clk(clk), .Q(s_out[2]));  // open: Qn, preset, reset
  Multiplexer multiplexer_3 (.in0(s_out[2]), .in1(inp[2]), .out(multiplexer_3_out), .sel(enble));
  D_Flip_Flop d_ff_4 (.D(multiplexer_4_out), .clk(clk), .Q(s_out[3]));  // open: Qn, preset, reset
  Multiplexer multiplexer_4 (.in0(s_out[3]), .in1(inp[3]), .out(multiplexer_4_out), .sel(enble));
  D_Flip_Flop d_ff_5 (.D(multiplexer_5_out), .clk(clk), .Q(s_out[4]));  // open: Qn, preset, reset
  Multiplexer multiplexer_5 (.in0(s_out[4]), .in1(inp[4]), .out(multiplexer_5_out), .sel(enble));
  D_Flip_Flop d_ff_6 (.D(multiplexer_6_out), .clk(clk), .Q(s_out[5]));  // open: Qn, preset, reset
  Multiplexer multiplexer_6 (.in0(s_out[5]), .in1(inp[5]), .out(multiplexer_6_out), .sel(enble));
  Multiplexer multiplexer_7 (.in0(s_out[6]), .in1(inp[6]), .out(multiplexer_7_out), .sel(enble));
  D_Flip_Flop d_ff_7 (.D(multiplexer_7_out), .clk(clk), .Q(s_out[6]));  // open: Qn, preset, reset
  Multiplexer multiplexer_8 (.in0(s_out[7]), .in1(inp[7]), .out(multiplexer_8_out), .sel(enble));
  D_Flip_Flop d_ff_8 (.D(multiplexer_8_out), .clk(clk), .Q(s_out[7]));  // open: Qn, preset, reset
endmodule

module contador (
  input  clk,
  output [2:0] sout
);

  wire d_ff_1_qn, d_ff_2_qn, d_ff_3_qn;

  D_Flip_Flop d_ff_1 (.D(d_ff_1_qn), .clk(clk), .Q(sout[0]), .Qn(d_ff_1_qn));  // open: preset, reset
  D_Flip_Flop d_ff_2 (.D(d_ff_2_qn), .clk(d_ff_1_qn), .Q(sout[1]), .Qn(d_ff_2_qn));  // open: preset, reset
  D_Flip_Flop d_ff_3 (.D(d_ff_3_qn), .clk(d_ff_2_qn), .Q(sout[2]), .Qn(d_ff_3_qn));  // open: preset, reset
endmodule

module celula (
  input  line_selector,
  input  dt,
  input  clk,
  output sout
);

  wire and_1_out, d_ff_1_q;

  and and_1 (and_1_out, line_selector, clk);
  D_Flip_Flop d_ff_1 (.D(dt), .clk(and_1_out), .Q(d_ff_1_q));  // open: Qn, preset, reset
  buf buffer_1 (sout, d_ff_1_q);
endmodule

module RAM_p (
  input  [7:0] dt,
  input  enable,
  input  clk,
  input  set,
  input  CS,
  input  [7:0] in_6,
  input  in_7,
  output [7:0] out_8
);

  wire decoder_1_out0, decoder_1_out1, decoder_1_out2, decoder_1_out3, decoder_2_out0, decoder_2_out1,
       decoder_2_out2, decoder_2_out3;
  wire [7:0] register_1_q;

  Register register_1 (.D(dt), .en(enable), .Q(register_1_q), .clk(clk));  // open: clr
  Decoder #(.enable("false"), .select(4)) decoder_1 (
    .out0(decoder_1_out0), .out1(decoder_1_out1), .out2(decoder_1_out2), .out3(decoder_1_out3),
    .sel(register_1_q[7:4]));  // open: out4, out5, out6, out7, out8, out9, out10, out11, out12, out13, out14, out15
  Decoder #(.enable("false"), .select(4)) decoder_2 (
    .out0(decoder_2_out0), .out1(decoder_2_out1), .out2(decoder_2_out2), .out3(decoder_2_out3),
    .sel(register_1_q[3:0]));  // open: out4, out5, out6, out7, out8, out9, out10, out11, out12, out13, out14, out15
  cell_memo cell_memo_1 (.dt_in(in_6), .x(decoder_1_out0), .y(decoder_2_out0), .set(set), .clk(CS), .dt_out(in_6));
  cell_memo cell_memo_2 (.dt_in(in_6), .x(decoder_1_out1), .y(decoder_2_out0), .set(set), .clk(CS), .dt_out(in_6));
  cell_memo cell_memo_3 (.dt_in(in_6), .x(decoder_1_out2), .y(decoder_2_out0), .set(set), .clk(CS), .dt_out(in_6));
  cell_memo cell_memo_4 (.dt_in(in_6), .x(decoder_1_out3), .y(decoder_2_out0), .set(set), .clk(CS), .dt_out(in_6));
  cell_memo cell_memo_5 (.dt_in(in_6), .x(decoder_1_out0), .y(decoder_2_out1), .set(set), .clk(CS), .dt_out(in_6));
  cell_memo cell_memo_6 (.dt_in(in_6), .x(decoder_1_out1), .y(decoder_2_out1), .set(set), .clk(CS), .dt_out(in_6));
  cell_memo cell_memo_7 (.dt_in(in_6), .x(decoder_1_out2), .y(decoder_2_out1), .set(set), .clk(CS), .dt_out(in_6));
  cell_memo cell_memo_8 (.dt_in(in_6), .x(decoder_1_out3), .y(decoder_2_out1), .set(set), .clk(CS), .dt_out(in_6));
  cell_memo cell_memo_9 (.dt_in(in_6), .x(decoder_1_out0), .y(decoder_2_out2), .set(set), .clk(CS), .dt_out(in_6));
  cell_memo cell_memo_10 (.dt_in(in_6), .x(decoder_1_out1), .y(decoder_2_out2), .set(set), .clk(CS), .dt_out(in_6));
  cell_memo cell_memo_11 (.dt_in(in_6), .x(decoder_1_out2), .y(decoder_2_out2), .set(set), .clk(CS), .dt_out(in_6));
  cell_memo cell_memo_12 (.dt_in(in_6), .x(decoder_1_out3), .y(decoder_2_out2), .set(set), .clk(CS), .dt_out(in_6));
  cell_memo cell_memo_13 (.dt_in(in_6), .x(decoder_1_out0), .y(decoder_2_out3), .set(set), .clk(CS), .dt_out(in_6));
  cell_memo cell_memo_14 (.dt_in(in_6), .x(decoder_1_out1), .y(decoder_2_out3), .set(set), .clk(CS), .dt_out(in_6));
  cell_memo cell_memo_15 (.dt_in(in_6), .x(decoder_1_out2), .y(decoder_2_out3), .set(set), .clk(CS), .dt_out(in_6));
  cell_memo cell_memo_16 (.dt_in(in_6), .x(decoder_1_out3), .y(decoder_2_out3), .set(set), .clk(CS), .dt_out(in_6));
  Register register_2 (.D(in_6), .Q(out_8), .clk(in_7));  // open: en, clr
endmodule

module reg8 (
  input  [7:0] sinput,
  input  set,
  input  endble,
  output [7:0] sout
);

  wire flpd_1_sout, flpd_2_sout, flpd_3_sout, flpd_4_sout, flpd_5_sout, flpd_6_sout, flpd_7_sout, flpd_8_sout;

  flpd flpd_1 (.iput(sinput[0]), .set(set), .sout(flpd_1_sout));
  flpd flpd_2 (.iput(sinput[1]), .set(set), .sout(flpd_2_sout));
  flpd flpd_3 (.iput(sinput[2]), .set(set), .sout(flpd_3_sout));
  flpd flpd_4 (.iput(sinput[3]), .set(set), .sout(flpd_4_sout));
  flpd flpd_5 (.iput(sinput[4]), .set(set), .sout(flpd_5_sout));
  flpd flpd_6 (.iput(sinput[5]), .set(set), .sout(flpd_6_sout));
  flpd flpd_7 (.iput(sinput[6]), .set(set), .sout(flpd_7_sout));
  flpd flpd_8 (.iput(sinput[7]), .set(set), .sout(flpd_8_sout));
  and and_1 (sout[0], flpd_1_sout, endble);
  and and_2 (sout[1], flpd_2_sout, endble);
  and and_3 (sout[2], flpd_3_sout, endble);
  and and_4 (sout[3], flpd_4_sout, endble);
  and and_5 (sout[4], flpd_5_sout, endble);
  and and_6 (sout[5], flpd_6_sout, endble);
  and and_7 (sout[6], flpd_7_sout, endble);
  and and_8 (sout[7], flpd_8_sout, endble);
endmodule

// 1b
module flpd (
  input  iput,
  input  set,
  output sout
);

  wire nand_1_out, nand_2_out, nand_4_out, not_1_out;

  not not_1 (not_1_out, iput);
  nand nand_1 (nand_1_out, iput, set);
  nand nand_2 (nand_2_out, set, not_1_out);
  nand nand_3 (sout, nand_1_out, nand_4_out);
  nand nand_4 (nand_4_out, sout, nand_2_out);
endmodule

// cell
module cell_memo (
  input  [7:0] dt_in,
  input  x,
  input  y,
  input  set,
  input  clk,
  output [7:0] dt_out
);

  wire and_1_out, and_2_out, and_3_out;
  wire [7:0] reg8_1_sout;

  and and_1 (and_1_out, x, y);
  and and_2 (and_2_out, and_1_out, set);
  and and_3 (and_3_out, and_1_out, clk);
  reg8 reg8_1 (.sinput(dt_in), .set(and_2_out), .endble(and_3_out), .sout(reg8_1_sout));
  assign dt_out = and_3_out ? reg8_1_sout : 8'bz;  // Controlled_Buffer controlled_buffer_1
endmodule

module ram_t (
  input  [7:0] A,
  input  clk,
  input  WE,
  input  [7:0] D,
  input  OE,
  output [7:0] out_6
);

  wire and_1_out, and_2_out, and_3_out, decoder_1_out0, decoder_1_out1, decoder_1_out2, decoder_1_out3,
       decoder_2_out0, decoder_2_out1, decoder_2_out2, decoder_2_out3, not_1_out, not_2_out;
  wire [7:0] buffer_1_out, buffer_2_out, buffer_3_out, buffer_4_out, buffer_5_out, buffer_6_out,
       buffer_7_out, cell_memo_1_dt_out, cell_memo_5_dt_out, cell_memo_9_dt_out, cell_memo_13_dt_out,
       controlled_buffer_1_out, register_1_q;

  not not_1 (not_1_out, OE);
  and and_1 (and_1_out, OE, clk);
  Register register_1 (.D(A), .en(clk), .Q(register_1_q), .clk(clk));  // open: clr
  and and_2 (and_2_out, WE, clk);
  and and_3 (and_3_out, clk, OE);
  assign controlled_buffer_1_out = not_1_out ? D : 8'bz;  // Controlled_Buffer controlled_buffer_1
  Decoder #(.enable("false"), .select(4)) decoder_1 (
    .out0(decoder_1_out0), .out1(decoder_1_out1), .out2(decoder_1_out2), .out3(decoder_1_out3),
    .sel(register_1_q[7:4]));  // open: out4, out5, out6, out7, out8, out9, out10, out11, out12, out13, out14, out15
  not not_2 (not_2_out, and_1_out);
  assign buffer_1_out = controlled_buffer_1_out;  // Buffer buffer_1, 8 bits wide
  Decoder #(.enable("false"), .select(4)) decoder_2 (
    .out0(decoder_2_out0), .out1(decoder_2_out1), .out2(decoder_2_out2), .out3(decoder_2_out3),
    .sel(register_1_q[3:0]));  // open: out4, out5, out6, out7, out8, out9, out10, out11, out12, out13, out14, out15
  cell_memo cell_memo_1 (
    .dt_in(buffer_1_out), .x(decoder_1_out0), .y(decoder_2_out0), .set(and_2_out), .clk(clk),
    .dt_out(cell_memo_1_dt_out));
  cell_memo cell_memo_2 (
    .dt_in(buffer_1_out), .x(decoder_1_out1), .y(decoder_2_out0), .set(and_2_out), .clk(clk),
    .dt_out(cell_memo_1_dt_out));
  cell_memo cell_memo_3 (
    .dt_in(buffer_1_out), .x(decoder_1_out2), .y(decoder_2_out0), .set(and_2_out), .clk(clk),
    .dt_out(cell_memo_1_dt_out));
  cell_memo cell_memo_4 (
    .dt_in(buffer_1_out), .x(decoder_1_out3), .y(decoder_2_out0), .set(and_2_out), .clk(clk),
    .dt_out(cell_memo_1_dt_out));
  assign buffer_2_out = buffer_3_out;  // Buffer buffer_2, 8 bits wide
  assign controlled_buffer_1_out = and_3_out ? cell_memo_1_dt_out : 8'bz;  // Controlled_Buffer controlled_buffer_2
  assign buffer_3_out = controlled_buffer_1_out;  // Buffer buffer_3, 8 bits wide
  cell_memo cell_memo_5 (
    .dt_in(buffer_2_out), .x(decoder_1_out0), .y(decoder_2_out1), .set(and_2_out), .clk(clk),
    .dt_out(cell_memo_5_dt_out));
  cell_memo cell_memo_6 (
    .dt_in(buffer_2_out), .x(decoder_1_out1), .y(decoder_2_out1), .set(and_2_out), .clk(clk),
    .dt_out(cell_memo_5_dt_out));
  cell_memo cell_memo_7 (
    .dt_in(buffer_2_out), .x(decoder_1_out2), .y(decoder_2_out1), .set(and_2_out), .clk(clk),
    .dt_out(cell_memo_5_dt_out));
  cell_memo cell_memo_8 (
    .dt_in(buffer_2_out), .x(decoder_1_out3), .y(decoder_2_out1), .set(and_2_out), .clk(clk),
    .dt_out(cell_memo_5_dt_out));
  assign buffer_3_out = and_3_out ? cell_memo_5_dt_out : 8'bz;  // Controlled_Buffer controlled_buffer_3
  assign buffer_4_out = buffer_5_out;  // Buffer buffer_4, 8 bits wide
  assign buffer_5_out = buffer_3_out;  // Buffer buffer_5, 8 bits wide
  cell_memo cell_memo_9 (
    .dt_in(buffer_4_out), .x(decoder_1_out0), .y(decoder_2_out2), .set(and_2_out), .clk(clk),
    .dt_out(cell_memo_9_dt_out));
  cell_memo cell_memo_10 (
    .dt_in(buffer_4_out), .x(decoder_1_out1), .y(decoder_2_out2), .set(and_2_out), .clk(clk),
    .dt_out(cell_memo_9_dt_out));
  cell_memo cell_memo_11 (
    .dt_in(buffer_4_out), .x(decoder_1_out2), .y(decoder_2_out2), .set(and_2_out), .clk(clk),
    .dt_out(cell_memo_9_dt_out));
  cell_memo cell_memo_12 (
    .dt_in(buffer_4_out), .x(decoder_1_out3), .y(decoder_2_out2), .set(and_2_out), .clk(clk),
    .dt_out(cell_memo_9_dt_out));
  assign buffer_5_out = and_3_out ? cell_memo_9_dt_out : 8'bz;  // Controlled_Buffer controlled_buffer_4
  assign buffer_6_out = buffer_7_out;  // Buffer buffer_6, 8 bits wide
  assign buffer_7_out = buffer_5_out;  // Buffer buffer_7, 8 bits wide
  cell_memo cell_memo_13 (
    .dt_in(buffer_6_out), .x(decoder_1_out0), .y(decoder_2_out3), .set(and_2_out), .clk(clk),
    .dt_out(cell_memo_13_dt_out));
  cell_memo cell_memo_14 (
    .dt_in(buffer_6_out), .x(decoder_1_out1), .y(decoder_2_out3), .set(and_2_out), .clk(clk),
    .dt_out(cell_memo_13_dt_out));
  cell_memo cell_memo_15 (
    .dt_in(buffer_6_out), .x(decoder_1_out2), .y(decoder_2_out3), .set(and_2_out), .clk(clk),
    .dt_out(cell_memo_13_dt_out));
  cell_memo cell_memo_16 (
    .dt_in(buffer_6_out), .x(decoder_1_out3), .y(decoder_2_out3), .set(and_2_out), .clk(clk),
    .dt_out(cell_memo_13_dt_out));
  assign buffer_7_out = and_3_out ? cell_memo_13_dt_out : 8'bz;  // Controlled_Buffer controlled_buffer_5
  Register register_2 (.D(buffer_7_out), .Q(out_6), .clk(not_2_out));  // open: en, clr
endmodule

module ram_v3 (
  input  [7:0] dt,
  input  enable,
  input  RWS,
  input  [7:0] in_4,
  input  OE,
  output [7:0] out_6
);

  wire and_1_out, and_2_out, clk, decoder_1_out0, decoder_1_out1, decoder_1_out2, decoder_1_out3,
       decoder_2_out0, decoder_2_out1, decoder_2_out2, decoder_2_out3, not_1_out, not_2_out;
  wire [3:0] mult;
  wire [7:0] buffer_1_out, buffer_2_out, buffer_3_out, buffer_4_out, cell_memo_1_dt_out, cell_memo_5_dt_out,
       cell_memo_9_dt_out, cell_memo_13_dt_out, controlled_buffer_1_out, controlled_buffer_2_out,
       controlled_buffer_3_out, controlled_buffer_4_out;
  wire [7:4] register_1_q;

  Clock clock_1 (.out(clk));
  not not_1 (not_1_out, RWS);
  Register register_1 (.D(dt), .en(enable), .Q({register_1_q, mult}), .clk(clk));  // open: clr
  and and_1 (and_1_out, RWS, clk);
  and and_2 (and_2_out, clk, not_1_out);
  assign controlled_buffer_1_out = and_1_out ? in_4 : 8'bz;  // Controlled_Buffer controlled_buffer_1
  Decoder #(.enable("false"), .select(4)) decoder_1 (
    .out0(decoder_1_out0), .out1(decoder_1_out1), .out2(decoder_1_out2), .out3(decoder_1_out3),
    .sel(register_1_q));  // open: out4, out5, out6, out7, out8, out9, out10, out11, out12, out13, out14, out15
  not not_2 (not_2_out, and_2_out);
  assign buffer_1_out = controlled_buffer_1_out;  // Buffer buffer_1, 8 bits wide
  Decoder #(.enable("false"), .select(4)) decoder_2 (
    .out0(decoder_2_out0), .out1(decoder_2_out1), .out2(decoder_2_out2), .out3(decoder_2_out3), .sel(mult));  // open: out4, out5, out6, out7, out8, out9, out10, out11, out12, out13, out14, out15
  cell_memo cell_memo_1 (
    .dt_in(buffer_1_out), .x(decoder_1_out0), .y(decoder_2_out0), .set(and_1_out), .clk(clk),
    .dt_out(cell_memo_1_dt_out));
  cell_memo cell_memo_2 (
    .dt_in(buffer_1_out), .x(decoder_1_out1), .y(decoder_2_out0), .set(and_1_out), .clk(clk),
    .dt_out(cell_memo_1_dt_out));
  cell_memo cell_memo_3 (
    .dt_in(buffer_1_out), .x(decoder_1_out2), .y(decoder_2_out0), .set(and_1_out), .clk(clk),
    .dt_out(cell_memo_1_dt_out));
  cell_memo cell_memo_4 (
    .dt_in(buffer_1_out), .x(decoder_1_out3), .y(decoder_2_out0), .set(and_1_out), .clk(clk),
    .dt_out(cell_memo_1_dt_out));
  assign buffer_2_out = controlled_buffer_1_out;  // Buffer buffer_2, 8 bits wide
  assign controlled_buffer_2_out = not_2_out ? cell_memo_1_dt_out : 8'bz;  // Controlled_Buffer controlled_buffer_2
  Multiplexer #(.enable("true"), .select(4), .width(8)) multiplexer_1 (
    .in0(controlled_buffer_2_out), .in1(cell_memo_5_dt_out), .in2(controlled_buffer_3_out),
    .in3(controlled_buffer_4_out), .out(out_6), .sel(mult), .en(OE));  // open: in4, in5, in6, in7, in8, in9, in10, in11, in12, in13, in14, in15
  cell_memo cell_memo_5 (
    .dt_in(buffer_2_out), .x(decoder_1_out0), .y(decoder_2_out1), .set(and_1_out), .clk(clk),
    .dt_out(cell_memo_5_dt_out));
  cell_memo cell_memo_6 (
    .dt_in(buffer_2_out), .x(decoder_1_out1), .y(decoder_2_out1), .set(and_1_out), .clk(clk),
    .dt_out(cell_memo_5_dt_out));
  cell_memo cell_memo_7 (
    .dt_in(buffer_2_out), .x(decoder_1_out2), .y(decoder_2_out1), .set(and_1_out), .clk(clk),
    .dt_out(cell_memo_5_dt_out));
  cell_memo cell_memo_8 (
    .dt_in(buffer_2_out), .x(decoder_1_out3), .y(decoder_2_out1), .set(and_1_out), .clk(clk),
    .dt_out(cell_memo_5_dt_out));
  assign buffer_3_out = controlled_buffer_1_out;  // Buffer buffer_3, 8 bits wide
  cell_memo cell_memo_9 (
    .dt_in(buffer_3_out), .x(decoder_1_out0), .y(decoder_2_out2), .set(and_1_out), .clk(clk),
    .dt_out(cell_memo_9_dt_out));
  cell_memo cell_memo_10 (
    .dt_in(buffer_3_out), .x(decoder_1_out1), .y(decoder_2_out2), .set(and_1_out), .clk(clk),
    .dt_out(cell_memo_9_dt_out));
  cell_memo cell_memo_11 (
    .dt_in(buffer_3_out), .x(decoder_1_out2), .y(decoder_2_out2), .set(and_1_out), .clk(clk),
    .dt_out(cell_memo_9_dt_out));
  cell_memo cell_memo_12 (
    .dt_in(buffer_3_out), .x(decoder_1_out3), .y(decoder_2_out2), .set(and_1_out), .clk(clk),
    .dt_out(cell_memo_9_dt_out));
  assign controlled_buffer_3_out = not_2_out ? cell_memo_9_dt_out : 8'bz;  // Controlled_Buffer controlled_buffer_3
  assign buffer_4_out = controlled_buffer_1_out;  // Buffer buffer_4, 8 bits wide
  cell_memo cell_memo_13 (
    .dt_in(buffer_4_out), .x(decoder_1_out0), .y(decoder_2_out3), .set(and_1_out), .clk(clk),
    .dt_out(cell_memo_13_dt_out));
  cell_memo cell_memo_14 (
    .dt_in(buffer_4_out), .x(decoder_1_out1), .y(decoder_2_out3), .set(and_1_out), .clk(clk),
    .dt_out(cell_memo_13_dt_out));
  cell_memo cell_memo_15 (
    .dt_in(buffer_4_out), .x(decoder_1_out2), .y(decoder_2_out3), .set(and_1_out), .clk(clk),
    .dt_out(cell_memo_13_dt_out));
  cell_memo cell_memo_16 (
    .dt_in(buffer_4_out), .x(decoder_1_out3), .y(decoder_2_out3), .set(and_1_out), .clk(clk),
    .dt_out(cell_memo_13_dt_out));
  assign controlled_buffer_4_out = not_2_out ? cell_memo_13_dt_out : 8'bz;  // Controlled_Buffer controlled_buffer_4
endmodule

module memo_test (
  input  [7:0] A,
  input  clk,
  input  WE,
  input  [7:0] D,
  input  OE,
  output [7:0] out_6
);

  wire and_1_out, and_2_out, and_3_out, and_4_out, and_5_out, and_6_out, decoder_1_out0, decoder_1_out1,
       decoder_1_out2, decoder_1_out3, decoder_2_out0, decoder_2_out1, decoder_2_out2, decoder_2_out3,
       not_1_out, not_2_out;
  wire [7:0] buffer_1_out, buffer_2_out, buffer_3_out, buffer_4_out, cell_memo_1_dt_out, cell_memo_5_dt_out,
       cell_memo_9_dt_out, cell_memo_13_dt_out, controlled_buffer_1_out, register_1_q;

  not not_1 (not_1_out, OE);
  and and_1 (and_1_out, OE, clk);
  Register register_1 (.D(A), .en(clk), .Q(register_1_q), .clk(clk));  // open: clr
  and and_2 (and_2_out, WE, clk);
  assign controlled_buffer_1_out = not_1_out ? D : 8'bz;  // Controlled_Buffer controlled_buffer_1
  Decoder #(.enable("false"), .select(4)) decoder_1 (
    .out0(decoder_1_out0), .out1(decoder_1_out1), .out2(decoder_1_out2), .out3(decoder_1_out3),
    .sel(register_1_q[7:4]));  // open: out4, out5, out6, out7, out8, out9, out10, out11, out12, out13, out14, out15
  not not_2 (not_2_out, and_1_out);
  assign buffer_1_out = controlled_buffer_1_out;  // Buffer buffer_1, 8 bits wide
  Decoder #(.enable("false"), .select(4)) decoder_2 (
    .out0(decoder_2_out0), .out1(decoder_2_out1), .out2(decoder_2_out2), .out3(decoder_2_out3),
    .sel(register_1_q[3:0]));  // open: out4, out5, out6, out7, out8, out9, out10, out11, out12, out13, out14, out15
  cell_memo cell_memo_1 (
    .dt_in(buffer_1_out), .x(decoder_1_out0), .y(decoder_2_out0), .set(and_2_out), .clk(clk),
    .dt_out(cell_memo_1_dt_out));
  cell_memo cell_memo_2 (
    .dt_in(buffer_1_out), .x(decoder_1_out1), .y(decoder_2_out0), .set(and_2_out), .clk(clk),
    .dt_out(cell_memo_1_dt_out));
  cell_memo cell_memo_3 (
    .dt_in(buffer_1_out), .x(decoder_1_out2), .y(decoder_2_out0), .set(and_2_out), .clk(clk),
    .dt_out(cell_memo_1_dt_out));
  cell_memo cell_memo_4 (
    .dt_in(buffer_1_out), .x(decoder_1_out3), .y(decoder_2_out0), .set(and_2_out), .clk(clk),
    .dt_out(cell_memo_1_dt_out));
  and and_3 (and_3_out, decoder_2_out0, OE);
  assign buffer_2_out = controlled_buffer_1_out;  // Buffer buffer_2, 8 bits wide
  assign controlled_buffer_1_out = and_3_out ? cell_memo_1_dt_out : 8'bz;  // Controlled_Buffer controlled_buffer_2
  cell_memo cell_memo_5 (
    .dt_in(buffer_2_out), .x(decoder_1_out0), .y(decoder_2_out1), .set(and_2_out), .clk(clk),
    .dt_out(cell_memo_5_dt_out));
  cell_memo cell_memo_6 (
    .dt_in(buffer_2_out), .x(decoder_1_out1), .y(decoder_2_out1), .set(and_2_out), .clk(clk),
    .dt_out(cell_memo_5_dt_out));
  cell_memo cell_memo_7 (
    .dt_in(buffer_2_out), .x(decoder_1_out2), .y(decoder_2_out1), .set(and_2_out), .clk(clk),
    .dt_out(cell_memo_5_dt_out));
  cell_memo cell_memo_8 (
    .dt_in(buffer_2_out), .x(decoder_1_out3), .y(decoder_2_out1), .set(and_2_out), .clk(clk),
    .dt_out(cell_memo_5_dt_out));
  and and_4 (and_4_out, decoder_2_out1, OE);
  assign controlled_buffer_1_out = and_4_out ? cell_memo_5_dt_out : 8'bz;  // Controlled_Buffer controlled_buffer_3
  assign buffer_3_out = controlled_buffer_1_out;  // Buffer buffer_3, 8 bits wide
  cell_memo cell_memo_9 (
    .dt_in(buffer_3_out), .x(decoder_1_out0), .y(decoder_2_out2), .set(and_2_out), .clk(clk),
    .dt_out(cell_memo_9_dt_out));
  cell_memo cell_memo_10 (
    .dt_in(buffer_3_out), .x(decoder_1_out1), .y(decoder_2_out2), .set(and_2_out), .clk(clk),
    .dt_out(cell_memo_9_dt_out));
  cell_memo cell_memo_11 (
    .dt_in(buffer_3_out), .x(decoder_1_out2), .y(decoder_2_out2), .set(and_2_out), .clk(clk),
    .dt_out(cell_memo_9_dt_out));
  cell_memo cell_memo_12 (
    .dt_in(buffer_3_out), .x(decoder_1_out3), .y(decoder_2_out2), .set(and_2_out), .clk(clk),
    .dt_out(cell_memo_9_dt_out));
  and and_5 (and_5_out, decoder_2_out2, OE);
  assign controlled_buffer_1_out = and_5_out ? cell_memo_9_dt_out : 8'bz;  // Controlled_Buffer controlled_buffer_4
  assign buffer_4_out = controlled_buffer_1_out;  // Buffer buffer_4, 8 bits wide
  cell_memo cell_memo_13 (
    .dt_in(buffer_4_out), .x(decoder_1_out0), .y(decoder_2_out3), .set(and_2_out), .clk(clk),
    .dt_out(cell_memo_13_dt_out));
  cell_memo cell_memo_14 (
    .dt_in(buffer_4_out), .x(decoder_1_out1), .y(decoder_2_out3), .set(and_2_out), .clk(clk),
    .dt_out(cell_memo_13_dt_out));
  cell_memo cell_memo_15 (
    .dt_in(buffer_4_out), .x(decoder_1_out2), .y(decoder_2_out3), .set(and_2_out), .clk(clk),
    .dt_out(cell_memo_13_dt_out));
  cell_memo cell_memo_16 (
    .dt_in(buffer_4_out), .x(decoder_1_out3), .y(decoder_2_out3), .set(and_2_out), .clk(clk),
    .dt_out(cell_memo_13_dt_out));
  and and_6 (and_6_out, decoder_2_out3, OE);
  assign controlled_buffer_1_out = and_6_out ? cell_memo_13_dt_out : 8'bz;  // Controlled_Buffer controlled_buffer_5
  Register register_2 (.D(controlled_buffer_1_out), .Q(out_6), .clk(not_2_out));  // open: en, clr
endmodule
