// Logisim project revisao.circ as structural Verilog: 6 circuits, main circuit main
module main (
  input  [7:0] in_1,
  input  [7:0] in_2,
  input  [15:0] in_3,
  input  [15:0] in_4,
  output [7:0] out_5,
  output [3:0] out_6,
  output [15:0] out_7,
  output [15:0] out_8
);

  wire adder_2_cout, clock_1_out, sum_8bits_1_c_out, sum_16bits_1_c_out;
  wire [3:0] adder_1_out;

  Clock clock_1 (.out(clock_1_out));
  Adder #(.width(4)) adder_1 (.a(4'b0000), .b(out_6), .out(adder_1_out));  // open: cin, cout
  redistrodor redistrodor_1 (.d(adder_1_out), .clk(clock_1_out), .s_out(out_6));
  sum_16bits sum_16bits_1 (.a(in_3), .b(in_4), .c_out(sum_16bits_1_c_out), .s_out(out_7));  // open: c_in
  LED led_1 (.in(sum_16bits_1_c_out));
  Adder #(.width(16)) adder_2 (.a(in_3), .b(in_4), .out(out_8), .cout(adder_2_cout));  // open: cin
  LED led_2 (.in(adder_2_cout));
  sum_8bits sum_8bits_1 (.a(in_1), .b(in_2), .c_out(sum_8bits_1_c_out), .s_out(out_5));  // open: c_in
  LED led_3 (.in(sum_8bits_1_c_out));
endmodule

module sum (
  input  c_in,
  input  a,
  input  b,
  output s_out,
  output c_out
);

  wire and_1_out, and_2_out, and_3_out, xor_1_out;

  xor xor_1 (xor_1_out, a, b);
  xor xor_2 (s_out, xor_1_out, c_in);
  and and_1 (and_1_out, a, c_in);
  and and_2 (and_2_out, b, c_in);
  and and_3 (and_3_out, a, b);
  or or_1 (c_out, and_1_out, and_2_out, and_3_out);
endmodule

module sum_8bits (
  input  c_in,
  input  [7:0] a,
  input  [7:0] b,
  output [7:0] s_out,
  output c_out
);

  wire sum_1_c_out, sum_2_c_out, sum_3_c_out, sum_4_c_out, sum_5_c_out, sum_6_c_out, sum_7_c_out;

  sum sum_1 (.a(a[0]), .b(b[0]), .c_in(c_in), .c_out(sum_1_c_out), .s_out(s_out[0]));
  sum sum_2 (.a(a[1]), .b(b[1]), .c_in(sum_1_c_out), .c_out(sum_2_c_out), .s_out(s_out[1]));
  sum sum_3 (.a(a[2]), .b(b[2]), .c_in(sum_2_c_out), .c_out(sum_3_c_out), .s_out(s_out[2]));
  sum sum_4 (.a(a[3]), .b(b[3]), .c_in(sum_3_c_out), .c_out(sum_4_c_out), .s_out(s_out[3]));
  sum sum_5 (.a(a[4]), .b(b[4]), .c_in(sum_4_c_out), .c_out(sum_5_c_out), .s_out(s_out[4]));
  sum sum_6 (.a(a[5]), .b(b[5]), .c_in(sum_5_c_out), .c_out(sum_6_c_out), .s_out(s_out[5]));
  sum sum_7 (.a(a[6]), .b(b[6]), .c_in(sum_6_c_out), .c_out(sum_7_c_out), .s_out(s_out[6]));
  sum sum_8 (.a(a[7]), .b(b[7]), .c_in(sum_7_c_out), .c_out(c_out), .s_out(s_out[7]));
endmodule

module sum_16bits (
  input  c_in,
  input  [15:0] a,
  input  [15:0] b,
  output [15:0] s_out,
  output c_out
);

  wire sum_8bits_1_c_out;

  sum_8bits sum_8bits_1 (.a(a[7:0]), .b(b[7:0]), .c_in(c_in), .c_out(sum_8bits_1_c_out), .s_out(s_out[7:0]));
  sum_8bits sum_8bits_2 (.a(a[15:8]), .b(b[15:8]), .c_in(sum_8bits_1_c_out), .c_out(c_out), .s_out(s_out[15:8]));
endmodule

module redistrodor (
  input  [3:0] d,
  input  clk,
  output [3:0] s_out
);

  D_Flip_Flop d_ff_1 (.D(d[0]), .clk(clk), .Q(s_out[0]));  // open: Qn, preset, reset
  D_Flip_Flop d_ff_2 (.D(d[1]), .clk(clk), .Q(s_out[1]));  // open: Qn, preset, reset
  D_Flip_Flop d_ff_3 (.D(d[2]), .clk(clk), .Q(s_out[2]));  // open: Qn, preset, reset
  D_Flip_Flop d_ff_4 (.D(d[3]), .clk(clk), .Q(s_out[3]));  // open: Qn, preset, reset
endmodule

module flip_flop_d (
  input  d,
  input  clk,
  output q,
  output q_b
);

  wire nand_1_out, nand_2_out, not_1_out;

  not not_1 (not_1_out, d);
  nand nand_1 (nand_1_out, d, clk);
  nand nand_2 (nand_2_out, clk, not_1_out);
  nand nand_3 (q, nand_1_out, q_b);
  nand nand_4 (q_b, q, nand_2_out);
endmodule
