// Logisim project flip_flop_jk.circ as structural Verilog: 1 circuit, main circuit main
module main (
  input  J,
  input  K,
  input  in_3,
  output out_4,
  output out_5,
  output out_6
);

  wire not_1_out, not_2_out, not_3_out;

  not not_1 (not_1_out, in_3);
  not not_2 (not_2_out, not_1_out);
  not not_3 (not_3_out, not_2_out);
  and and_1 (out_6, in_3, not_3_out);
  J_K_Flip_Flop #(.trigger("falling")) j_k_ff_1 (
    .J(J), .K(K), .clk(out_6), .Q(out_4), .Qn(out_5));  // open: preset, reset

  // Notes on the sheet:
  //   Dector de bordas de subida.
endmodule
