// Logisim project flip_flop_rs.circ as structural Verilog: 1 circuit, main circuit main
module main (
  input  S,
  input  in_2,
  input  R,
  output Q,
  output out_5,
  output Q_2
);

  wire nand_1_out, nand_2_out, not_1_out, not_2_out, not_3_out;

  not not_1 (not_1_out, in_2);
  not not_2 (not_2_out, not_1_out);
  not not_3 (not_3_out, not_2_out);
  and and_1 (out_5, in_2, not_3_out);
  nand nand_1 (nand_1_out, S, out_5);
  nand nand_2 (nand_2_out, out_5, R);
  nand nand_3 (Q, nand_1_out, Q_2);
  nand nand_4 (Q_2, Q, nand_2_out);

  // Notes on the sheet:
  //   Dector de bordas de subida.
endmodule
