// Logisim project lauch_rs.circ as structural Verilog: 1 circuit, main circuit main
module main (
  input  S,
  input  R,
  output Q,
  output Q_2
);

  wire nand_1_out, nand_2_out;

  not nand_1 (nand_1_out, S);  // NAND_Gate
  not nand_2 (nand_2_out, R);  // NAND_Gate
  nand nand_3 (Q, nand_1_out, Q_2);
  nand nand_4 (Q_2, Q, nand_2_out);
endmodule
